// Logisim project mips.circ as structural Verilog: 17 circuits, main circuit Reg32
module Reg32 (
  input  RegWrite,
  input  [4:0] WP,
  input  CK,
  input  [31:0] Data,
  input  [4:0] RP1,
  input  [4:0] RP2,
  output [31:0] RDATA1,
  output [31:0] RDATA2
);

  wire decoder_1_out0, decoder_1_out1, decoder_1_out2, decoder_1_out3, decoder_1_out4, decoder_1_out5,
       decoder_1_out6, decoder_1_out7, decoder_2_out0, decoder_2_out1, decoder_2_out2, decoder_2_out3,
       decoder_3_out0, decoder_3_out1, decoder_3_out2, decoder_3_out3, decoder_4_out0, decoder_4_out1,
       decoder_4_out2, decoder_4_out3, decoder_5_out0, decoder_5_out1, decoder_5_out2, decoder_5_out3,
       decoder_6_out0, decoder_6_out1, decoder_6_out2, decoder_6_out3, decoder_7_out0, decoder_7_out1,
       decoder_7_out2, decoder_7_out3, decoder_8_out0, decoder_8_out1, decoder_8_out2, decoder_8_out3,
       decoder_9_out0, decoder_9_out1, decoder_9_out2, decoder_9_out3;
  wire [3:0] register_2_q, register_2_q_2, register_2_q_3, register_2_q_4, register_2_q_5, register_2_q_6,
       register_2_q_7, register_2_q_8, register_3_q, register_3_q_2, register_3_q_3, register_3_q_4,
       register_3_q_5, register_3_q_6, register_3_q_7, register_3_q_8, register_4_q, register_4_q_2,
       register_4_q_3, register_4_q_4, register_4_q_5, register_4_q_6, register_4_q_7, register_4_q_8,
       register_5_q, register_5_q_2, register_5_q_3, register_5_q_4, register_5_q_5, register_5_q_6,
       register_5_q_7, register_5_q_8, register_6_q, register_6_q_2, register_6_q_3, register_6_q_4,
       register_6_q_5, register_6_q_6, register_6_q_7, register_6_q_8, register_7_q, register_7_q_2,
       register_7_q_3, register_7_q_4, register_7_q_5, register_7_q_6, register_7_q_7, register_7_q_8,
       register_8_q, register_8_q_2, register_8_q_3, register_8_q_4, register_8_q_5, register_8_q_6,
       register_8_q_7, register_8_q_8, register_9_q, register_9_q_2, register_9_q_3, register_9_q_4,
       register_9_q_5, register_9_q_6, register_9_q_7, register_9_q_8, register_10_q, register_10_q_2,
       register_10_q_3, register_10_q_4, register_10_q_5, register_10_q_6, register_10_q_7, register_10_q_8,
       register_11_q, register_11_q_2, register_11_q_3, register_11_q_4, register_11_q_5, register_11_q_6,
       register_11_q_7, register_11_q_8, register_12_q, register_12_q_2, register_12_q_3, register_12_q_4,
       register_12_q_5, register_12_q_6, register_12_q_7, register_12_q_8, register_13_q, register_13_q_2,
       register_13_q_3, register_13_q_4, register_13_q_5, register_13_q_6, register_13_q_7, register_13_q_8,
       register_14_q, register_14_q_2, register_14_q_3, register_14_q_4, register_14_q_5, register_14_q_6,
       register_14_q_7, register_14_q_8, register_15_q, register_15_q_2, register_15_q_3, register_15_q_4,
       register_15_q_5, register_15_q_6, register_15_q_7, register_15_q_8, register_16_q, register_16_q_2,
       register_16_q_3, register_16_q_4, register_16_q_5, register_16_q_6, register_16_q_7, register_16_q_8,
       register_17_q, register_17_q_2, register_17_q_3, register_17_q_4, register_17_q_5, register_17_q_6,
       register_17_q_7, register_17_q_8, register_18_q, register_18_q_2, register_18_q_3, register_18_q_4,
       register_18_q_5, register_18_q_6, register_18_q_7, register_18_q_8, register_19_q, register_19_q_2,
       register_19_q_3, register_19_q_4, register_19_q_5, register_19_q_6, register_19_q_7, register_19_q_8,
       register_20_q, register_20_q_2, register_20_q_3, register_20_q_4, register_20_q_5, register_20_q_6,
       register_20_q_7, register_20_q_8, register_21_q, register_21_q_2, register_21_q_3, register_21_q_4,
       register_21_q_5, register_21_q_6, register_21_q_7, register_21_q_8, register_22_q, register_22_q_2,
       register_22_q_3, register_22_q_4, register_22_q_5, register_22_q_6, register_22_q_7, register_22_q_8,
       register_23_q, register_23_q_2, register_23_q_3, register_23_q_4, register_23_q_5, register_23_q_6,
       register_23_q_7, register_23_q_8, register_24_q, register_24_q_2, register_24_q_3, register_24_q_4,
       register_24_q_5, register_24_q_6, register_24_q_7, register_24_q_8, register_29_q, register_29_q_2,
       register_29_q_3, register_29_q_4, register_29_q_5, register_29_q_6, register_29_q_7, register_29_q_8,
       register_30_q, register_30_q_2, register_30_q_3, register_30_q_4, register_30_q_5, register_30_q_6,
       register_30_q_7, register_30_q_8;
  wire [31:0] multiplexer_1_out, multiplexer_2_out, multiplexer_3_out, multiplexer_4_out, multiplexer_5_out,
       multiplexer_6_out, multiplexer_7_out, multiplexer_8_out, multiplexer_9_out, multiplexer_10_out,
       multiplexer_11_out, multiplexer_12_out, multiplexer_13_out, multiplexer_14_out, multiplexer_15_out,
       multiplexer_16_out, register_25_q, register_26_q, register_27_q, register_28_q, register_31_q,
       register_32_q;

  Decoder #(.select(3), .disabled(0)) decoder_1 (
    .out0(decoder_1_out0), .out1(decoder_1_out1), .out2(decoder_1_out2), .out3(decoder_1_out3),
    .out4(decoder_1_out4), .out5(decoder_1_out5), .out6(decoder_1_out6), .out7(decoder_1_out7),
    .sel(WP[2:0]), .en(RegWrite));
  Decoder #(.select(2), .disabled(0)) decoder_2 (
    .out0(decoder_2_out0), .out1(decoder_2_out1), .out2(decoder_2_out2), .out3(decoder_2_out3),
    .sel(WP[4:3]), .en(decoder_1_out0));
  Decoder #(.select(2), .disabled(0)) decoder_3 (
    .out0(decoder_3_out0), .out1(decoder_3_out1), .out2(decoder_3_out2), .out3(decoder_3_out3),
    .sel(WP[4:3]), .en(decoder_1_out1));
  Register #(.width(32)) register_1 (.D(Data), .en(decoder_2_out0), .clk(CK));  // open: Q, clr
  Register #(.width(32)) register_2 (
    .D(Data), .en(decoder_2_out1),
    .Q({register_2_q_8, register_2_q_7, register_2_q_6, register_2_q_5, register_2_q_4, register_2_q_3, register_2_q_2, register_2_q}),
    .clk(CK));  // open: clr
  Register #(.width(32)) register_3 (
    .D(Data), .en(decoder_2_out2),
    .Q({register_3_q_8, register_3_q_7, register_3_q_6, register_3_q_5, register_3_q_4, register_3_q_3, register_3_q_2, register_3_q}),
    .clk(CK));  // open: clr
  Register #(.width(32)) register_4 (
    .D(Data), .en(decoder_2_out3),
    .Q({register_4_q_8, register_4_q_7, register_4_q_6, register_4_q_5, register_4_q_4, register_4_q_3, register_4_q_2, register_4_q}),
    .clk(CK));  // open: clr
  Decoder #(.select(2), .disabled(0)) decoder_4 (
    .out0(decoder_4_out0), .out1(decoder_4_out1), .out2(decoder_4_out2), .out3(decoder_4_out3),
    .sel(WP[4:3]), .en(decoder_1_out2));
  Register #(.width(32)) register_5 (
    .D(Data), .en(decoder_3_out0),
    .Q({register_5_q_8, register_5_q_7, register_5_q_6, register_5_q_5, register_5_q_4, register_5_q_3, register_5_q_2, register_5_q}),
    .clk(CK));  // open: clr
  Register #(.width(32)) register_6 (
    .D(Data), .en(decoder_3_out1),
    .Q({register_6_q_8, register_6_q_7, register_6_q_6, register_6_q_5, register_6_q_4, register_6_q_3, register_6_q_2, register_6_q}),
    .clk(CK));  // open: clr
  Register #(.width(32)) register_7 (
    .D(Data), .en(decoder_3_out2),
    .Q({register_7_q_8, register_7_q_7, register_7_q_6, register_7_q_5, register_7_q_4, register_7_q_3, register_7_q_2, register_7_q}),
    .clk(CK));  // open: clr
  Register #(.width(32)) register_8 (
    .D(Data), .en(decoder_3_out3),
    .Q({register_8_q_8, register_8_q_7, register_8_q_6, register_8_q_5, register_8_q_4, register_8_q_3, register_8_q_2, register_8_q}),
    .clk(CK));  // open: clr
  Multiplexer #(.select(2), .width(32), .enable("false")) multiplexer_1 (
    .in0({32{1'b0}}),
    .in1({register_2_q_8, register_2_q_7, register_2_q_6, register_2_q_5, register_2_q_4, register_2_q_3, register_2_q_2, register_2_q}),
    .in2({register_3_q_8, register_3_q_7, register_3_q_6, register_3_q_5, register_3_q_4, register_3_q_3, register_3_q_2, register_3_q}),
    .in3({register_4_q_8, register_4_q_7, register_4_q_6, register_4_q_5, register_4_q_4, register_4_q_3, register_4_q_2, register_4_q}),
    .out(multiplexer_1_out), .sel(RP1[4:3]));
  Multiplexer #(.select(2), .width(32), .enable("false")) multiplexer_2 (
    .in0({32{1'b0}}),
    .in1({register_2_q_8, register_2_q_7, register_2_q_6, register_2_q_5, register_2_q_4, register_2_q_3, register_2_q_2, register_2_q}),
    .in2({register_3_q_8, register_3_q_7, register_3_q_6, register_3_q_5, register_3_q_4, register_3_q_3, register_3_q_2, register_3_q}),
    .in3({register_4_q_8, register_4_q_7, register_4_q_6, register_4_q_5, register_4_q_4, register_4_q_3, register_4_q_2, register_4_q}),
    .out(multiplexer_2_out), .sel(RP2[4:3]));
  Multiplexer #(.select(2), .width(32), .enable("false")) multiplexer_3 (
    .in0({register_5_q_8, register_5_q_7, register_5_q_6, register_5_q_5, register_5_q_4, register_5_q_3, register_5_q_2, register_5_q}),
    .in1({register_6_q_8, register_6_q_7, register_6_q_6, register_6_q_5, register_6_q_4, register_6_q_3, register_6_q_2, register_6_q}),
    .in2({register_7_q_8, register_7_q_7, register_7_q_6, register_7_q_5, register_7_q_4, register_7_q_3, register_7_q_2, register_7_q}),
    .in3({register_8_q_8, register_8_q_7, register_8_q_6, register_8_q_5, register_8_q_4, register_8_q_3, register_8_q_2, register_8_q}),
    .out(multiplexer_3_out), .sel(RP1[4:3]));
  Multiplexer #(.select(2), .width(32), .enable("false")) multiplexer_4 (
    .in0({register_5_q_8, register_5_q_7, register_5_q_6, register_5_q_5, register_5_q_4, register_5_q_3, register_5_q_2, register_5_q}),
    .in1({register_6_q_8, register_6_q_7, register_6_q_6, register_6_q_5, register_6_q_4, register_6_q_3, register_6_q_2, register_6_q}),
    .in2({register_7_q_8, register_7_q_7, register_7_q_6, register_7_q_5, register_7_q_4, register_7_q_3, register_7_q_2, register_7_q}),
    .in3({register_8_q_8, register_8_q_7, register_8_q_6, register_8_q_5, register_8_q_4, register_8_q_3, register_8_q_2, register_8_q}),
    .out(multiplexer_4_out), .sel(RP2[4:3]));
  Decoder #(.select(2), .disabled(0)) decoder_5 (
    .out0(decoder_5_out0), .out1(decoder_5_out1), .out2(decoder_5_out2), .out3(decoder_5_out3),
    .sel(WP[4:3]), .en(decoder_1_out3));
  Register #(.width(32)) register_9 (
    .D(Data), .en(decoder_4_out0),
    .Q({register_9_q_8, register_9_q_7, register_9_q_6, register_9_q_5, register_9_q_4, register_9_q_3, register_9_q_2, register_9_q}),
    .clk(CK));  // open: clr
  Register #(.width(32)) register_10 (
    .D(Data), .en(decoder_4_out1),
    .Q({register_10_q_8, register_10_q_7, register_10_q_6, register_10_q_5, register_10_q_4, register_10_q_3, register_10_q_2, register_10_q}),
    .clk(CK));  // open: clr
  Register #(.width(32)) register_11 (
    .D(Data), .en(decoder_4_out2),
    .Q({register_11_q_8, register_11_q_7, register_11_q_6, register_11_q_5, register_11_q_4, register_11_q_3, register_11_q_2, register_11_q}),
    .clk(CK));  // open: clr
  Register #(.width(32)) register_12 (
    .D(Data), .en(decoder_4_out3),
    .Q({register_12_q_8, register_12_q_7, register_12_q_6, register_12_q_5, register_12_q_4, register_12_q_3, register_12_q_2, register_12_q}),
    .clk(CK));  // open: clr
  Register #(.width(32)) register_13 (
    .D(Data), .en(decoder_5_out0),
    .Q({register_13_q_8, register_13_q_7, register_13_q_6, register_13_q_5, register_13_q_4, register_13_q_3, register_13_q_2, register_13_q}),
    .clk(CK));  // open: clr
  Register #(.width(32)) register_14 (
    .D(Data), .en(decoder_5_out1),
    .Q({register_14_q_8, register_14_q_7, register_14_q_6, register_14_q_5, register_14_q_4, register_14_q_3, register_14_q_2, register_14_q}),
    .clk(CK));  // open: clr
  Register #(.width(32)) register_15 (
    .D(Data), .en(decoder_5_out2),
    .Q({register_15_q_8, register_15_q_7, register_15_q_6, register_15_q_5, register_15_q_4, register_15_q_3, register_15_q_2, register_15_q}),
    .clk(CK));  // open: clr
  Register #(.width(32)) register_16 (
    .D(Data), .en(decoder_5_out3),
    .Q({register_16_q_8, register_16_q_7, register_16_q_6, register_16_q_5, register_16_q_4, register_16_q_3, register_16_q_2, register_16_q}),
    .clk(CK));  // open: clr
  Multiplexer #(.select(2), .width(32), .enable("false")) multiplexer_5 (
    .in0({register_9_q_8, register_9_q_7, register_9_q_6, register_9_q_5, register_9_q_4, register_9_q_3, register_9_q_2, register_9_q}),
    .in1({register_10_q_8, register_10_q_7, register_10_q_6, register_10_q_5, register_10_q_4, register_10_q_3, register_10_q_2, register_10_q}),
    .in2({register_11_q_8, register_11_q_7, register_11_q_6, register_11_q_5, register_11_q_4, register_11_q_3, register_11_q_2, register_11_q}),
    .in3({register_12_q_8, register_12_q_7, register_12_q_6, register_12_q_5, register_12_q_4, register_12_q_3, register_12_q_2, register_12_q}),
    .out(multiplexer_5_out), .sel(RP1[4:3]));
  Multiplexer #(.select(2), .width(32), .enable("false")) multiplexer_6 (
    .in0({register_9_q_8, register_9_q_7, register_9_q_6, register_9_q_5, register_9_q_4, register_9_q_3, register_9_q_2, register_9_q}),
    .in1({register_10_q_8, register_10_q_7, register_10_q_6, register_10_q_5, register_10_q_4, register_10_q_3, register_10_q_2, register_10_q}),
    .in2({register_11_q_8, register_11_q_7, register_11_q_6, register_11_q_5, register_11_q_4, register_11_q_3, register_11_q_2, register_11_q}),
    .in3({register_12_q_8, register_12_q_7, register_12_q_6, register_12_q_5, register_12_q_4, register_12_q_3, register_12_q_2, register_12_q}),
    .out(multiplexer_6_out), .sel(RP2[4:3]));
  Decoder #(.select(2), .disabled(0)) decoder_6 (
    .out0(decoder_6_out0), .out1(decoder_6_out1), .out2(decoder_6_out2), .out3(decoder_6_out3),
    .sel(WP[4:3]), .en(decoder_1_out4));
  Decoder #(.select(2), .disabled(0)) decoder_7 (
    .out0(decoder_7_out0), .out1(decoder_7_out1), .out2(decoder_7_out2), .out3(decoder_7_out3),
    .sel(WP[4:3]), .en(decoder_1_out5));
  Register #(.width(32)) register_17 (
    .D(Data), .en(decoder_6_out0),
    .Q({register_17_q_8, register_17_q_7, register_17_q_6, register_17_q_5, register_17_q_4, register_17_q_3, register_17_q_2, register_17_q}),
    .clk(CK));  // open: clr
  Register #(.width(32)) register_18 (
    .D(Data), .en(decoder_6_out1),
    .Q({register_18_q_8, register_18_q_7, register_18_q_6, register_18_q_5, register_18_q_4, register_18_q_3, register_18_q_2, register_18_q}),
    .clk(CK));  // open: clr
  Register #(.width(32)) register_19 (
    .D(Data), .en(decoder_6_out2),
    .Q({register_19_q_8, register_19_q_7, register_19_q_6, register_19_q_5, register_19_q_4, register_19_q_3, register_19_q_2, register_19_q}),
    .clk(CK));  // open: clr
  Register #(.width(32)) register_20 (
    .D(Data), .en(decoder_6_out3),
    .Q({register_20_q_8, register_20_q_7, register_20_q_6, register_20_q_5, register_20_q_4, register_20_q_3, register_20_q_2, register_20_q}),
    .clk(CK));  // open: clr
  Multiplexer #(.select(2), .width(32), .enable("false")) multiplexer_7 (
    .in0({register_13_q_8, register_13_q_7, register_13_q_6, register_13_q_5, register_13_q_4, register_13_q_3, register_13_q_2, register_13_q}),
    .in1({register_14_q_8, register_14_q_7, register_14_q_6, register_14_q_5, register_14_q_4, register_14_q_3, register_14_q_2, register_14_q}),
    .in2({register_15_q_8, register_15_q_7, register_15_q_6, register_15_q_5, register_15_q_4, register_15_q_3, register_15_q_2, register_15_q}),
    .in3({register_16_q_8, register_16_q_7, register_16_q_6, register_16_q_5, register_16_q_4, register_16_q_3, register_16_q_2, register_16_q}),
    .out(multiplexer_7_out), .sel(RP1[4:3]));
  Multiplexer #(.select(2), .width(32), .enable("false")) multiplexer_8 (
    .in0({register_13_q_8, register_13_q_7, register_13_q_6, register_13_q_5, register_13_q_4, register_13_q_3, register_13_q_2, register_13_q}),
    .in1({register_14_q_8, register_14_q_7, register_14_q_6, register_14_q_5, register_14_q_4, register_14_q_3, register_14_q_2, register_14_q}),
    .in2({register_15_q_8, register_15_q_7, register_15_q_6, register_15_q_5, register_15_q_4, register_15_q_3, register_15_q_2, register_15_q}),
    .in3({register_16_q_8, register_16_q_7, register_16_q_6, register_16_q_5, register_16_q_4, register_16_q_3, register_16_q_2, register_16_q}),
    .out(multiplexer_8_out), .sel(RP2[4:3]));
  Multiplexer #(.select(2), .width(32), .enable("false")) multiplexer_9 (
    .in0({register_17_q_8, register_17_q_7, register_17_q_6, register_17_q_5, register_17_q_4, register_17_q_3, register_17_q_2, register_17_q}),
    .in1({register_18_q_8, register_18_q_7, register_18_q_6, register_18_q_5, register_18_q_4, register_18_q_3, register_18_q_2, register_18_q}),
    .in2({register_19_q_8, register_19_q_7, register_19_q_6, register_19_q_5, register_19_q_4, register_19_q_3, register_19_q_2, register_19_q}),
    .in3({register_20_q_8, register_20_q_7, register_20_q_6, register_20_q_5, register_20_q_4, register_20_q_3, register_20_q_2, register_20_q}),
    .out(multiplexer_9_out), .sel(RP1[4:3]));
  Multiplexer #(.select(2), .width(32), .enable("false")) multiplexer_10 (
    .in0({register_17_q_8, register_17_q_7, register_17_q_6, register_17_q_5, register_17_q_4, register_17_q_3, register_17_q_2, register_17_q}),
    .in1({register_18_q_8, register_18_q_7, register_18_q_6, register_18_q_5, register_18_q_4, register_18_q_3, register_18_q_2, register_18_q}),
    .in2({register_19_q_8, register_19_q_7, register_19_q_6, register_19_q_5, register_19_q_4, register_19_q_3, register_19_q_2, register_19_q}),
    .in3({register_20_q_8, register_20_q_7, register_20_q_6, register_20_q_5, register_20_q_4, register_20_q_3, register_20_q_2, register_20_q}),
    .out(multiplexer_10_out), .sel(RP2[4:3]));
  Decoder #(.select(2), .disabled(0)) decoder_8 (
    .out0(decoder_8_out0), .out1(decoder_8_out1), .out2(decoder_8_out2), .out3(decoder_8_out3),
    .sel(WP[4:3]), .en(decoder_1_out6));
  Register #(.width(32)) register_21 (
    .D(Data), .en(decoder_7_out0),
    .Q({register_21_q_8, register_21_q_7, register_21_q_6, register_21_q_5, register_21_q_4, register_21_q_3, register_21_q_2, register_21_q}),
    .clk(CK));  // open: clr
  Register #(.width(32)) register_22 (
    .D(Data), .en(decoder_7_out1),
    .Q({register_22_q_8, register_22_q_7, register_22_q_6, register_22_q_5, register_22_q_4, register_22_q_3, register_22_q_2, register_22_q}),
    .clk(CK));  // open: clr
  Register #(.width(32)) register_23 (
    .D(Data), .en(decoder_7_out2),
    .Q({register_23_q_8, register_23_q_7, register_23_q_6, register_23_q_5, register_23_q_4, register_23_q_3, register_23_q_2, register_23_q}),
    .clk(CK));  // open: clr
  Register #(.width(32)) register_24 (
    .D(Data), .en(decoder_7_out3),
    .Q({register_24_q_8, register_24_q_7, register_24_q_6, register_24_q_5, register_24_q_4, register_24_q_3, register_24_q_2, register_24_q}),
    .clk(CK));  // open: clr
  Decoder #(.select(2), .disabled(0)) decoder_9 (
    .out0(decoder_9_out0), .out1(decoder_9_out1), .out2(decoder_9_out2), .out3(decoder_9_out3),
    .sel(WP[4:3]), .en(decoder_1_out7));
  Register #(.width(32)) register_25 (.D(Data), .en(decoder_8_out0), .Q(register_25_q), .clk(CK));  // open: clr
  Register #(.width(32)) register_26 (.D(Data), .en(decoder_8_out1), .Q(register_26_q), .clk(CK));  // open: clr
  Register #(.width(32)) register_27 (.D(Data), .en(decoder_8_out2), .Q(register_27_q), .clk(CK));  // open: clr
  Register #(.width(32)) register_28 (.D(Data), .en(decoder_8_out3), .Q(register_28_q), .clk(CK));  // open: clr
  Multiplexer #(.select(2), .width(32), .enable("false")) multiplexer_11 (
    .in0({register_21_q_8, register_21_q_7, register_21_q_6, register_21_q_5, register_21_q_4, register_21_q_3, register_21_q_2, register_21_q}),
    .in1({register_22_q_8, register_22_q_7, register_22_q_6, register_22_q_5, register_22_q_4, register_22_q_3, register_22_q_2, register_22_q}),
    .in2({register_23_q_8, register_23_q_7, register_23_q_6, register_23_q_5, register_23_q_4, register_23_q_3, register_23_q_2, register_23_q}),
    .in3({register_24_q_8, register_24_q_7, register_24_q_6, register_24_q_5, register_24_q_4, register_24_q_3, register_24_q_2, register_24_q}),
    .out(multiplexer_11_out), .sel(RP1[4:3]));
  Multiplexer #(.select(2), .width(32), .enable("false")) multiplexer_12 (
    .in0({register_21_q_8, register_21_q_7, register_21_q_6, register_21_q_5, register_21_q_4, register_21_q_3, register_21_q_2, register_21_q}),
    .in1({register_22_q_8, register_22_q_7, register_22_q_6, register_22_q_5, register_22_q_4, register_22_q_3, register_22_q_2, register_22_q}),
    .in2({register_23_q_8, register_23_q_7, register_23_q_6, register_23_q_5, register_23_q_4, register_23_q_3, register_23_q_2, register_23_q}),
    .in3({register_24_q_8, register_24_q_7, register_24_q_6, register_24_q_5, register_24_q_4, register_24_q_3, register_24_q_2, register_24_q}),
    .out(multiplexer_12_out), .sel(RP2[4:3]));
  Register #(.width(32)) register_29 (
    .D(Data), .en(decoder_9_out0),
    .Q({register_29_q_8, register_29_q_7, register_29_q_6, register_29_q_5, register_29_q_4, register_29_q_3, register_29_q_2, register_29_q}),
    .clk(CK));  // open: clr
  Register #(.width(32)) register_30 (
    .D(Data), .en(decoder_9_out1),
    .Q({register_30_q_8, register_30_q_7, register_30_q_6, register_30_q_5, register_30_q_4, register_30_q_3, register_30_q_2, register_30_q}),
    .clk(CK));  // open: clr
  Register #(.width(32)) register_31 (.D(Data), .en(decoder_9_out2), .Q(register_31_q), .clk(CK));  // open: clr
  Register #(.width(32)) register_32 (.D(Data), .en(decoder_9_out3), .Q(register_32_q), .clk(CK));  // open: clr
  Multiplexer #(.select(2), .width(32), .enable("false")) multiplexer_13 (
    .in0(register_25_q), .in1(register_26_q), .in2(register_27_q), .in3(register_28_q),
    .out(multiplexer_13_out), .sel(RP1[4:3]));
  Multiplexer #(.select(2), .width(32), .enable("false")) multiplexer_14 (
    .in0(register_25_q), .in1(register_26_q), .in2(register_27_q), .in3(register_28_q),
    .out(multiplexer_14_out), .sel(RP2[4:3]));
  Hex_Digit_Display hex_digit_display_1 (.value(4'b0000));  // open: dp
  Hex_Digit_Display hex_digit_display_2 (.value(register_2_q_8));  // open: dp
  Hex_Digit_Display hex_digit_display_3 (.value(register_3_q_8));  // open: dp
  Hex_Digit_Display hex_digit_display_4 (.value(register_4_q_8));  // open: dp
  Multiplexer #(.select(2), .width(32), .enable("false")) multiplexer_15 (
    .in0({register_29_q_8, register_29_q_7, register_29_q_6, register_29_q_5, register_29_q_4, register_29_q_3, register_29_q_2, register_29_q}),
    .in1({register_30_q_8, register_30_q_7, register_30_q_6, register_30_q_5, register_30_q_4, register_30_q_3, register_30_q_2, register_30_q}),
    .in2(register_31_q), .in3(register_32_q), .out(multiplexer_15_out), .sel(RP1[4:3]));
  Multiplexer #(.select(2), .width(32), .enable("false")) multiplexer_16 (
    .in0({register_29_q_8, register_29_q_7, register_29_q_6, register_29_q_5, register_29_q_4, register_29_q_3, register_29_q_2, register_29_q}),
    .in1({register_30_q_8, register_30_q_7, register_30_q_6, register_30_q_5, register_30_q_4, register_30_q_3, register_30_q_2, register_30_q}),
    .in2(register_31_q), .in3(register_32_q), .out(multiplexer_16_out), .sel(RP2[4:3]));
  Hex_Digit_Display hex_digit_display_5 (.value(4'b0000));  // open: dp
  Hex_Digit_Display hex_digit_display_6 (.value(4'b0000));  // open: dp
  Hex_Digit_Display hex_digit_display_7 (.value(register_2_q_6));  // open: dp
  Hex_Digit_Display hex_digit_display_8 (.value(register_2_q_7));  // open: dp
  Hex_Digit_Display hex_digit_display_9 (.value(register_3_q_7));  // open: dp
  Hex_Digit_Display hex_digit_display_10 (.value(register_3_q_6));  // open: dp
  Hex_Digit_Display hex_digit_display_11 (.value(register_4_q_7));  // open: dp
  Hex_Digit_Display hex_digit_display_12 (.value(register_4_q_6));  // open: dp
  Multiplexer #(.select(3), .width(32), .enable("false")) multiplexer_17 (
    .in0(multiplexer_1_out), .in1(multiplexer_3_out), .in2(multiplexer_5_out), .in3(multiplexer_7_out),
    .in4(multiplexer_9_out), .in5(multiplexer_11_out), .in6(multiplexer_13_out), .in7(multiplexer_15_out),
    .out(RDATA1), .sel(RP1[2:0]));
  Multiplexer #(.select(3), .width(32), .enable("false")) multiplexer_18 (
    .in0(multiplexer_2_out), .in1(multiplexer_4_out), .in2(multiplexer_6_out), .in3(multiplexer_8_out),
    .in4(multiplexer_10_out), .in5(multiplexer_12_out), .in6(multiplexer_14_out), .in7(multiplexer_16_out),
    .out(RDATA2), .sel(RP2[2:0]));
  Hex_Digit_Display hex_digit_display_13 (.value(4'b0000));  // open: dp
  Hex_Digit_Display hex_digit_display_14 (.value(4'b0000));  // open: dp
  Hex_Digit_Display hex_digit_display_15 (.value(register_2_q_4));  // open: dp
  Hex_Digit_Display hex_digit_display_16 (.value(register_2_q_5));  // open: dp
  Hex_Digit_Display hex_digit_display_17 (.value(register_3_q_5));  // open: dp
  Hex_Digit_Display hex_digit_display_18 (.value(register_3_q_4));  // open: dp
  Hex_Digit_Display hex_digit_display_19 (.value(register_4_q_4));  // open: dp
  Hex_Digit_Display hex_digit_display_20 (.value(register_4_q_5));  // open: dp
  Hex_Digit_Display hex_digit_display_21 (.value(4'b0000));  // open: dp
  Hex_Digit_Display hex_digit_display_22 (.value(4'b0000));  // open: dp
  Hex_Digit_Display hex_digit_display_23 (.value(register_2_q_2));  // open: dp
  Hex_Digit_Display hex_digit_display_24 (.value(register_2_q_3));  // open: dp
  Hex_Digit_Display hex_digit_display_25 (.value(register_3_q_2));  // open: dp
  Hex_Digit_Display hex_digit_display_26 (.value(register_3_q_3));  // open: dp
  Hex_Digit_Display hex_digit_display_27 (.value(register_4_q_2));  // open: dp
  Hex_Digit_Display hex_digit_display_28 (.value(register_4_q_3));  // open: dp
  Hex_Digit_Display hex_digit_display_29 (.value(4'b0000));  // open: dp
  Hex_Digit_Display hex_digit_display_30 (.value(register_2_q));  // open: dp
  Hex_Digit_Display hex_digit_display_31 (.value(register_3_q));  // open: dp
  Hex_Digit_Display hex_digit_display_32 (.value(register_4_q));  // open: dp
  Hex_Digit_Display hex_digit_display_33 (.value(register_5_q_8));  // open: dp
  Hex_Digit_Display hex_digit_display_34 (.value(register_5_q_7));  // open: dp
  Hex_Digit_Display hex_digit_display_35 (.value(register_6_q_7));  // open: dp
  Hex_Digit_Display hex_digit_display_36 (.value(register_6_q_8));  // open: dp
  Hex_Digit_Display hex_digit_display_37 (.value(register_7_q_7));  // open: dp
  Hex_Digit_Display hex_digit_display_38 (.value(register_7_q_8));  // open: dp
  Hex_Digit_Display hex_digit_display_39 (.value(register_8_q_8));  // open: dp
  Hex_Digit_Display hex_digit_display_40 (.value(register_8_q_7));  // open: dp
  Hex_Digit_Display hex_digit_display_41 (.value(register_5_q_5));  // open: dp
  Hex_Digit_Display hex_digit_display_42 (.value(register_5_q_6));  // open: dp
  Hex_Digit_Display hex_digit_display_43 (.value(register_6_q_5));  // open: dp
  Hex_Digit_Display hex_digit_display_44 (.value(register_6_q_6));  // open: dp
  Hex_Digit_Display hex_digit_display_45 (.value(register_7_q_5));  // open: dp
  Hex_Digit_Display hex_digit_display_46 (.value(register_7_q_6));  // open: dp
  Hex_Digit_Display hex_digit_display_47 (.value(register_8_q_5));  // open: dp
  Hex_Digit_Display hex_digit_display_48 (.value(register_8_q_6));  // open: dp
  Hex_Digit_Display hex_digit_display_49 (.value(register_5_q_3));  // open: dp
  Hex_Digit_Display hex_digit_display_50 (.value(register_5_q_4));  // open: dp
  Hex_Digit_Display hex_digit_display_51 (.value(register_6_q_3));  // open: dp
  Hex_Digit_Display hex_digit_display_52 (.value(register_6_q_4));  // open: dp
  Hex_Digit_Display hex_digit_display_53 (.value(register_7_q_4));  // open: dp
  Hex_Digit_Display hex_digit_display_54 (.value(register_7_q_3));  // open: dp
  Hex_Digit_Display hex_digit_display_55 (.value(register_8_q_3));  // open: dp
  Hex_Digit_Display hex_digit_display_56 (.value(register_8_q_4));  // open: dp
  Hex_Digit_Display hex_digit_display_57 (.value(register_5_q_2));  // open: dp
  Hex_Digit_Display hex_digit_display_58 (.value(register_5_q));  // open: dp
  Hex_Digit_Display hex_digit_display_59 (.value(register_6_q_2));  // open: dp
  Hex_Digit_Display hex_digit_display_60 (.value(register_6_q));  // open: dp
  Hex_Digit_Display hex_digit_display_61 (.value(register_7_q_2));  // open: dp
  Hex_Digit_Display hex_digit_display_62 (.value(register_7_q));  // open: dp
  Hex_Digit_Display hex_digit_display_63 (.value(register_8_q));  // open: dp
  Hex_Digit_Display hex_digit_display_64 (.value(register_8_q_2));  // open: dp
  Hex_Digit_Display hex_digit_display_65 (.value(register_9_q_7));  // open: dp
  Hex_Digit_Display hex_digit_display_66 (.value(register_9_q_8));  // open: dp
  Hex_Digit_Display hex_digit_display_67 (.value(register_10_q_8));  // open: dp
  Hex_Digit_Display hex_digit_display_68 (.value(register_10_q_7));  // open: dp
  Hex_Digit_Display hex_digit_display_69 (.value(register_11_q_7));  // open: dp
  Hex_Digit_Display hex_digit_display_70 (.value(register_11_q_8));  // open: dp
  Hex_Digit_Display hex_digit_display_71 (.value(register_12_q_8));  // open: dp
  Hex_Digit_Display hex_digit_display_72 (.value(register_12_q_7));  // open: dp
  Hex_Digit_Display hex_digit_display_73 (.value(register_9_q_6));  // open: dp
  Hex_Digit_Display hex_digit_display_74 (.value(register_9_q_5));  // open: dp
  Hex_Digit_Display hex_digit_display_75 (.value(register_10_q_6));  // open: dp
  Hex_Digit_Display hex_digit_display_76 (.value(register_10_q_5));  // open: dp
  Hex_Digit_Display hex_digit_display_77 (.value(register_11_q_6));  // open: dp
  Hex_Digit_Display hex_digit_display_78 (.value(register_11_q_5));  // open: dp
  Hex_Digit_Display hex_digit_display_79 (.value(register_12_q_6));  // open: dp
  Hex_Digit_Display hex_digit_display_80 (.value(register_12_q_5));  // open: dp
  Hex_Digit_Display hex_digit_display_81 (.value(register_9_q_4));  // open: dp
  Hex_Digit_Display hex_digit_display_82 (.value(register_9_q_3));  // open: dp
  Hex_Digit_Display hex_digit_display_83 (.value(register_10_q_3));  // open: dp
  Hex_Digit_Display hex_digit_display_84 (.value(register_10_q_4));  // open: dp
  Hex_Digit_Display hex_digit_display_85 (.value(register_11_q_4));  // open: dp
  Hex_Digit_Display hex_digit_display_86 (.value(register_11_q_3));  // open: dp
  Hex_Digit_Display hex_digit_display_87 (.value(register_12_q_3));  // open: dp
  Hex_Digit_Display hex_digit_display_88 (.value(register_12_q_4));  // open: dp
  Hex_Digit_Display hex_digit_display_89 (.value(register_9_q_2));  // open: dp
  Hex_Digit_Display hex_digit_display_90 (.value(register_9_q));  // open: dp
  Hex_Digit_Display hex_digit_display_91 (.value(register_10_q));  // open: dp
  Hex_Digit_Display hex_digit_display_92 (.value(register_10_q_2));  // open: dp
  Hex_Digit_Display hex_digit_display_93 (.value(register_11_q_2));  // open: dp
  Hex_Digit_Display hex_digit_display_94 (.value(register_11_q));  // open: dp
  Hex_Digit_Display hex_digit_display_95 (.value(register_12_q));  // open: dp
  Hex_Digit_Display hex_digit_display_96 (.value(register_12_q_2));  // open: dp
  Hex_Digit_Display hex_digit_display_97 (.value(register_13_q_8));  // open: dp
  Hex_Digit_Display hex_digit_display_98 (.value(register_14_q_8));  // open: dp
  Hex_Digit_Display hex_digit_display_99 (.value(register_15_q_8));  // open: dp
  Hex_Digit_Display hex_digit_display_100 (.value(register_16_q_8));  // open: dp
  Hex_Digit_Display hex_digit_display_101 (.value(register_13_q_7));  // open: dp
  Hex_Digit_Display hex_digit_display_102 (.value(register_13_q_6));  // open: dp
  Hex_Digit_Display hex_digit_display_103 (.value(register_14_q_6));  // open: dp
  Hex_Digit_Display hex_digit_display_104 (.value(register_14_q_7));  // open: dp
  Hex_Digit_Display hex_digit_display_105 (.value(register_15_q_6));  // open: dp
  Hex_Digit_Display hex_digit_display_106 (.value(register_15_q_7));  // open: dp
  Hex_Digit_Display hex_digit_display_107 (.value(register_16_q_7));  // open: dp
  Hex_Digit_Display hex_digit_display_108 (.value(register_16_q_6));  // open: dp
  Hex_Digit_Display hex_digit_display_109 (.value(register_13_q_5));  // open: dp
  Hex_Digit_Display hex_digit_display_110 (.value(register_13_q_4));  // open: dp
  Hex_Digit_Display hex_digit_display_111 (.value(register_14_q_5));  // open: dp
  Hex_Digit_Display hex_digit_display_112 (.value(register_14_q_4));  // open: dp
  Hex_Digit_Display hex_digit_display_113 (.value(register_15_q_5));  // open: dp
  Hex_Digit_Display hex_digit_display_114 (.value(register_15_q_4));  // open: dp
  Hex_Digit_Display hex_digit_display_115 (.value(register_16_q_4));  // open: dp
  Hex_Digit_Display hex_digit_display_116 (.value(register_16_q_5));  // open: dp
  Hex_Digit_Display hex_digit_display_117 (.value(register_13_q_3));  // open: dp
  Hex_Digit_Display hex_digit_display_118 (.value(register_13_q_2));  // open: dp
  Hex_Digit_Display hex_digit_display_119 (.value(register_14_q_3));  // open: dp
  Hex_Digit_Display hex_digit_display_120 (.value(register_14_q_2));  // open: dp
  Hex_Digit_Display hex_digit_display_121 (.value(register_15_q_3));  // open: dp
  Hex_Digit_Display hex_digit_display_122 (.value(register_15_q_2));  // open: dp
  Hex_Digit_Display hex_digit_display_123 (.value(register_16_q_2));  // open: dp
  Hex_Digit_Display hex_digit_display_124 (.value(register_16_q_3));  // open: dp
  Hex_Digit_Display hex_digit_display_125 (.value(register_13_q));  // open: dp
  Hex_Digit_Display hex_digit_display_126 (.value(register_14_q));  // open: dp
  Hex_Digit_Display hex_digit_display_127 (.value(register_15_q));  // open: dp
  Hex_Digit_Display hex_digit_display_128 (.value(register_16_q));  // open: dp
  Hex_Digit_Display hex_digit_display_129 (.value(register_17_q_8));  // open: dp
  Hex_Digit_Display hex_digit_display_130 (.value(register_17_q_7));  // open: dp
  Hex_Digit_Display hex_digit_display_131 (.value(register_18_q_7));  // open: dp
  Hex_Digit_Display hex_digit_display_132 (.value(register_18_q_8));  // open: dp
  Hex_Digit_Display hex_digit_display_133 (.value(register_19_q_8));  // open: dp
  Hex_Digit_Display hex_digit_display_134 (.value(register_19_q_7));  // open: dp
  Hex_Digit_Display hex_digit_display_135 (.value(register_20_q_7));  // open: dp
  Hex_Digit_Display hex_digit_display_136 (.value(register_20_q_8));  // open: dp
  Hex_Digit_Display hex_digit_display_137 (.value(register_17_q_6));  // open: dp
  Hex_Digit_Display hex_digit_display_138 (.value(register_17_q_5));  // open: dp
  Hex_Digit_Display hex_digit_display_139 (.value(register_18_q_6));  // open: dp
  Hex_Digit_Display hex_digit_display_140 (.value(register_18_q_5));  // open: dp
  Hex_Digit_Display hex_digit_display_141 (.value(register_19_q_5));  // open: dp
  Hex_Digit_Display hex_digit_display_142 (.value(register_19_q_6));  // open: dp
  Hex_Digit_Display hex_digit_display_143 (.value(register_20_q_6));  // open: dp
  Hex_Digit_Display hex_digit_display_144 (.value(register_20_q_5));  // open: dp
  Hex_Digit_Display hex_digit_display_145 (.value(register_17_q_3));  // open: dp
  Hex_Digit_Display hex_digit_display_146 (.value(register_17_q_4));  // open: dp
  Hex_Digit_Display hex_digit_display_147 (.value(register_18_q_3));  // open: dp
  Hex_Digit_Display hex_digit_display_148 (.value(register_18_q_4));  // open: dp
  Hex_Digit_Display hex_digit_display_149 (.value(register_19_q_3));  // open: dp
  Hex_Digit_Display hex_digit_display_150 (.value(register_19_q_4));  // open: dp
  Hex_Digit_Display hex_digit_display_151 (.value(register_20_q_4));  // open: dp
  Hex_Digit_Display hex_digit_display_152 (.value(register_20_q_3));  // open: dp
  Hex_Digit_Display hex_digit_display_153 (.value(register_17_q_2));  // open: dp
  Hex_Digit_Display hex_digit_display_154 (.value(register_17_q));  // open: dp
  Hex_Digit_Display hex_digit_display_155 (.value(register_18_q));  // open: dp
  Hex_Digit_Display hex_digit_display_156 (.value(register_18_q_2));  // open: dp
  Hex_Digit_Display hex_digit_display_157 (.value(register_19_q));  // open: dp
  Hex_Digit_Display hex_digit_display_158 (.value(register_19_q_2));  // open: dp
  Hex_Digit_Display hex_digit_display_159 (.value(register_20_q_2));  // open: dp
  Hex_Digit_Display hex_digit_display_160 (.value(register_20_q));  // open: dp
  Hex_Digit_Display hex_digit_display_161 (.value(register_21_q_8));  // open: dp
  Hex_Digit_Display hex_digit_display_162 (.value(register_22_q_8));  // open: dp
  Hex_Digit_Display hex_digit_display_163 (.value(register_23_q_8));  // open: dp
  Hex_Digit_Display hex_digit_display_164 (.value(register_24_q_8));  // open: dp
  Hex_Digit_Display hex_digit_display_165 (.value(register_21_q_7));  // open: dp
  Hex_Digit_Display hex_digit_display_166 (.value(register_21_q_6));  // open: dp
  Hex_Digit_Display hex_digit_display_167 (.value(register_22_q_7));  // open: dp
  Hex_Digit_Display hex_digit_display_168 (.value(register_22_q_6));  // open: dp
  Hex_Digit_Display hex_digit_display_169 (.value(register_23_q_7));  // open: dp
  Hex_Digit_Display hex_digit_display_170 (.value(register_23_q_6));  // open: dp
  Hex_Digit_Display hex_digit_display_171 (.value(register_24_q_7));  // open: dp
  Hex_Digit_Display hex_digit_display_172 (.value(register_24_q_6));  // open: dp
  Hex_Digit_Display hex_digit_display_173 (.value(register_21_q_5));  // open: dp
  Hex_Digit_Display hex_digit_display_174 (.value(register_21_q_4));  // open: dp
  Hex_Digit_Display hex_digit_display_175 (.value(register_22_q_5));  // open: dp
  Hex_Digit_Display hex_digit_display_176 (.value(register_22_q_4));  // open: dp
  Hex_Digit_Display hex_digit_display_177 (.value(register_23_q_4));  // open: dp
  Hex_Digit_Display hex_digit_display_178 (.value(register_23_q_5));  // open: dp
  Hex_Digit_Display hex_digit_display_179 (.value(register_24_q_4));  // open: dp
  Hex_Digit_Display hex_digit_display_180 (.value(register_24_q_5));  // open: dp
  Hex_Digit_Display hex_digit_display_181 (.value(register_21_q_3));  // open: dp
  Hex_Digit_Display hex_digit_display_182 (.value(register_21_q_2));  // open: dp
  Hex_Digit_Display hex_digit_display_183 (.value(register_22_q_2));  // open: dp
  Hex_Digit_Display hex_digit_display_184 (.value(register_22_q_3));  // open: dp
  Hex_Digit_Display hex_digit_display_185 (.value(register_23_q_2));  // open: dp
  Hex_Digit_Display hex_digit_display_186 (.value(register_23_q_3));  // open: dp
  Hex_Digit_Display hex_digit_display_187 (.value(register_24_q_2));  // open: dp
  Hex_Digit_Display hex_digit_display_188 (.value(register_24_q_3));  // open: dp
  Hex_Digit_Display hex_digit_display_189 (.value(register_25_q[31:28]));  // open: dp
  Hex_Digit_Display hex_digit_display_190 (.value(register_21_q));  // open: dp
  Hex_Digit_Display hex_digit_display_191 (.value(register_22_q));  // open: dp
  Hex_Digit_Display hex_digit_display_192 (.value(register_26_q[31:28]));  // open: dp
  Hex_Digit_Display hex_digit_display_193 (.value(register_27_q[31:28]));  // open: dp
  Hex_Digit_Display hex_digit_display_194 (.value(register_23_q));  // open: dp
  Hex_Digit_Display hex_digit_display_195 (.value(register_24_q));  // open: dp
  Hex_Digit_Display hex_digit_display_196 (.value(register_28_q[31:28]));  // open: dp
  Hex_Digit_Display hex_digit_display_197 (.value(register_25_q[23:20]));  // open: dp
  Hex_Digit_Display hex_digit_display_198 (.value(register_25_q[27:24]));  // open: dp
  Hex_Digit_Display hex_digit_display_199 (.value(register_26_q[27:24]));  // open: dp
  Hex_Digit_Display hex_digit_display_200 (.value(register_26_q[23:20]));  // open: dp
  Hex_Digit_Display hex_digit_display_201 (.value(register_27_q[23:20]));  // open: dp
  Hex_Digit_Display hex_digit_display_202 (.value(register_27_q[27:24]));  // open: dp
  Hex_Digit_Display hex_digit_display_203 (.value(register_28_q[27:24]));  // open: dp
  Hex_Digit_Display hex_digit_display_204 (.value(register_28_q[23:20]));  // open: dp
  Hex_Digit_Display hex_digit_display_205 (.value(register_25_q[15:12]));  // open: dp
  Hex_Digit_Display hex_digit_display_206 (.value(register_25_q[19:16]));  // open: dp
  Hex_Digit_Display hex_digit_display_207 (.value(register_26_q[15:12]));  // open: dp
  Hex_Digit_Display hex_digit_display_208 (.value(register_26_q[19:16]));  // open: dp
  Hex_Digit_Display hex_digit_display_209 (.value(register_27_q[19:16]));  // open: dp
  Hex_Digit_Display hex_digit_display_210 (.value(register_27_q[15:12]));  // open: dp
  Hex_Digit_Display hex_digit_display_211 (.value(register_28_q[19:16]));  // open: dp
  Hex_Digit_Display hex_digit_display_212 (.value(register_28_q[15:12]));  // open: dp
  Hex_Digit_Display hex_digit_display_213 (.value(register_25_q[11:8]));  // open: dp
  Hex_Digit_Display hex_digit_display_214 (.value(register_25_q[7:4]));  // open: dp
  Hex_Digit_Display hex_digit_display_215 (.value(register_26_q[11:8]));  // open: dp
  Hex_Digit_Display hex_digit_display_216 (.value(register_26_q[7:4]));  // open: dp
  Hex_Digit_Display hex_digit_display_217 (.value(register_27_q[7:4]));  // open: dp
  Hex_Digit_Display hex_digit_display_218 (.value(register_27_q[11:8]));  // open: dp
  Hex_Digit_Display hex_digit_display_219 (.value(register_28_q[11:8]));  // open: dp
  Hex_Digit_Display hex_digit_display_220 (.value(register_28_q[7:4]));  // open: dp
  Hex_Digit_Display hex_digit_display_221 (.value(register_25_q[3:0]));  // open: dp
  Hex_Digit_Display hex_digit_display_222 (.value(register_26_q[3:0]));  // open: dp
  Hex_Digit_Display hex_digit_display_223 (.value(register_27_q[3:0]));  // open: dp
  Hex_Digit_Display hex_digit_display_224 (.value(register_28_q[3:0]));  // open: dp
  Hex_Digit_Display hex_digit_display_225 (.value(register_29_q_8));  // open: dp
  Hex_Digit_Display hex_digit_display_226 (.value(register_29_q_7));  // open: dp
  Hex_Digit_Display hex_digit_display_227 (.value(register_30_q_8));  // open: dp
  Hex_Digit_Display hex_digit_display_228 (.value(register_30_q_7));  // open: dp
  Hex_Digit_Display hex_digit_display_229 (.value(register_31_q[31:28]));  // open: dp
  Hex_Digit_Display hex_digit_display_230 (.value(register_31_q[27:24]));  // open: dp
  Hex_Digit_Display hex_digit_display_231 (.value(register_32_q[27:24]));  // open: dp
  Hex_Digit_Display hex_digit_display_232 (.value(register_32_q[31:28]));  // open: dp
  Hex_Digit_Display hex_digit_display_233 (.value(register_29_q_6));  // open: dp
  Hex_Digit_Display hex_digit_display_234 (.value(register_29_q_5));  // open: dp
  Hex_Digit_Display hex_digit_display_235 (.value(register_30_q_6));  // open: dp
  Hex_Digit_Display hex_digit_display_236 (.value(register_30_q_5));  // open: dp
  Hex_Digit_Display hex_digit_display_237 (.value(register_31_q[23:20]));  // open: dp
  Hex_Digit_Display hex_digit_display_238 (.value(register_31_q[19:16]));  // open: dp
  Hex_Digit_Display hex_digit_display_239 (.value(register_32_q[23:20]));  // open: dp
  Hex_Digit_Display hex_digit_display_240 (.value(register_32_q[19:16]));  // open: dp
  Hex_Digit_Display hex_digit_display_241 (.value(register_29_q_3));  // open: dp
  Hex_Digit_Display hex_digit_display_242 (.value(register_29_q_4));  // open: dp
  Hex_Digit_Display hex_digit_display_243 (.value(register_30_q_4));  // open: dp
  Hex_Digit_Display hex_digit_display_244 (.value(register_30_q_3));  // open: dp
  Hex_Digit_Display hex_digit_display_245 (.value(register_31_q[15:12]));  // open: dp
  Hex_Digit_Display hex_digit_display_246 (.value(register_31_q[11:8]));  // open: dp
  Hex_Digit_Display hex_digit_display_247 (.value(register_32_q[15:12]));  // open: dp
  Hex_Digit_Display hex_digit_display_248 (.value(register_32_q[11:8]));  // open: dp
  Hex_Digit_Display hex_digit_display_249 (.value(register_29_q));  // open: dp
  Hex_Digit_Display hex_digit_display_250 (.value(register_29_q_2));  // open: dp
  Hex_Digit_Display hex_digit_display_251 (.value(register_30_q_2));  // open: dp
  Hex_Digit_Display hex_digit_display_252 (.value(register_30_q));  // open: dp
  Hex_Digit_Display hex_digit_display_253 (.value(register_31_q[7:4]));  // open: dp
  Hex_Digit_Display hex_digit_display_254 (.value(register_31_q[3:0]));  // open: dp
  Hex_Digit_Display hex_digit_display_255 (.value(register_32_q[3:0]));  // open: dp
  Hex_Digit_Display hex_digit_display_256 (.value(register_32_q[7:4]));  // open: dp

  // Notes on the sheet:
  //   0
  //   8
  //   16
  //   1
  //   7
  //   $zero
  //   $t0
  //   $s0
  //   $t8
  //   $at
  //   $t1
  //   $s1
  //   $t9
  //   $v0
  //   $t2
  //   $s2
  //   $k0
  //   $v1
  //   $t3
  //   $s3
  //   $k1
  //   $a0
  //   $t4
  //   $s4
  //   $gp
  //   $a1
  //   $t5
  //   $s5
  //   $sp
  //   $a2
  //   $t6
  //   $s6
  //   $fp
  //   $a3
  //   $t7
  //   $s7
  //   $ra
endmodule

module mainc_2 (
  input  [5:0] Op,
  output Jump,
  output Branch,
  output ALUSrc,
  output MemRead,
  output MemWrite,
  output MemtoRead,
  output RegDst,
  output RegWrite,
  output [1:0] ALUOp
);

  wire and_3_out, and_5_out, and_6_out;

  and and_1 (MemRead, Op[0], Op[1], ~Op[2], ~Op[3], ~Op[4], Op[5]);  // AND_Gate
  and and_2 (MemWrite, Op[0], Op[1], ~Op[2], Op[3], ~Op[4], Op[5]);  // AND_Gate
  and and_3 (and_3_out, Op[0], ~Op[1], Op[2], ~Op[3], ~Op[4], ~Op[5]);  // AND_Gate
  and and_4 (ALUOp[1], ~Op[0], ~Op[1], ~Op[2], ~Op[3], ~Op[4], ~Op[5]);  // AND_Gate
  and and_5 (and_5_out, ~Op[0], ~Op[1], ~Op[2], Op[3], ~Op[4], ~Op[5]);  // AND_Gate
  and and_6 (and_6_out, ~Op[0], ~Op[1], Op[2], ~Op[3], ~Op[4], ~Op[5]);  // AND_Gate
  and and_7 (Jump, ~Op[0], Op[1], ~Op[2], ~Op[3], ~Op[4], ~Op[5]);  // AND_Gate
  or or_1 (ALUSrc, MemRead, and_5_out, MemWrite);
  or or_2 (ALUOp[0], and_3_out, and_6_out);
  or or_3 (RegWrite, MemRead, and_5_out, ALUOp[1]);

  assign Branch = ALUOp[0];
  assign MemtoRead = MemRead;
  assign RegDst = ALUOp[1];

  // Notes on the sheet:
  //   lw
  //   sw
  //   bne
  //   R
  //   beq
  //   j
  //   addi
endmodule

module aluc_2 (
  input  [5:0] Func,
  input  [1:0] ALUOp,
  output [4:0] ALUfunc
);

  wire and_2_out, and_3_out, and_4_out, and_5_out, and_6_out, and_7_out;

  and and_1 (ALUfunc[3], Func[0], Func[1], Func[2], ~Func[3], ~Func[4], Func[5], ~ALUOp[0], ALUOp[1]);  // AND_Gate
  and and_2 (and_2_out, ~Func[0], Func[1], Func[2], ~Func[3], ~Func[4], Func[5], ~ALUOp[0], ALUOp[1]);  // AND_Gate
  and and_3 (and_3_out, ~Func[0], Func[1], ~Func[2], ~Func[3], ~Func[4], Func[5], ~ALUOp[0], ALUOp[1]);  // AND_Gate
  and and_4 (and_4_out, ALUOp[0], ~ALUOp[1]);  // AND_Gate
  and and_5 (and_5_out, ~Func[0], ~Func[1], ~Func[2], ~Func[3], ~Func[4], Func[5], ~ALUOp[0], ALUOp[1]);  // AND_Gate
  and and_6 (and_6_out, ~ALUOp[0], ~ALUOp[1]);  // AND_Gate
  and and_7 (and_7_out, Func[0], ~Func[1], Func[2], ~Func[3], ~Func[4], Func[5], ~ALUOp[0], ALUOp[1]);  // AND_Gate
  and and_8 (ALUfunc[4], ~Func[0], Func[1], ~Func[2], Func[3], ~Func[4], Func[5], ~ALUOp[0], ALUOp[1]);  // AND_Gate
  or or_1 (ALUfunc[2], ALUfunc[3], and_2_out, ALUfunc[4], and_3_out, and_4_out);
  or or_2 (ALUfunc[1], and_4_out, and_2_out, and_6_out, and_3_out, and_5_out, ALUfunc[4]);
  or or_3 (ALUfunc[0], and_2_out, and_7_out);
endmodule

module alu32_2 (
  input  Cin,
  input  [31:0] B,
  input  [31:0] A,
  input  [4:0] S,
  output [31:0] X,
  output NZ,
  output Cout
);

  wire nor_2_out;
  wire [31:0] adder_1_out, and_1_out, bit_extender_1_out, multiplexer_1_out, nor_1_out, or_1_out, xor_1_out,
       xor_2_out;

  assign bit_extender_1_out = {{31{S[2]}}, S[2]};  // Bit_Extender bit_extender_1
  assign and_1_out = A & B;  // AND_Gate and_1, 32 bits wide
  assign or_1_out = A | B;  // OR_Gate or_1, 32 bits wide
  assign xor_1_out = A ^ B;  // XOR_Gate xor_1, 32 bits wide
  assign nor_1_out = ~(A | B);  // NOR_Gate nor_1, 32 bits wide
  assign xor_2_out = bit_extender_1_out ^ B;  // XOR_Gate xor_2, 32 bits wide
  Adder #(.width(32)) adder_1 (.a(xor_2_out), .b(A), .out(adder_1_out), .cin(Cin), .cout(Cout));
  Multiplexer #(.select(3), .width(32), .enable("false")) multiplexer_1 (
    .in0(and_1_out), .in1(or_1_out), .in2(adder_1_out), .in3(xor_1_out), .in4(nor_1_out),
    .out(multiplexer_1_out), .sel({S[3], S[1:0]}));  // open: in5, in6, in7
  Multiplexer #(.width(32), .enable("false")) multiplexer_2 (
    .in0(multiplexer_1_out), .in1({{31{1'b1}}, multiplexer_1_out[31]}), .out(X), .sel(S[4]));
  not not_1 (NZ, nor_2_out);
  nor nor_2 (nor_2_out, X[0], X[1], X[2], X[3], X[4], X[5], X[6], X[7], X[8], X[9], X[10], X[11], X[12], X[13], X[14], X[15], X[17], X[18], X[19], X[20], X[21], X[22], X[23], X[24], X[25], X[26], X[27], X[28], X[29], X[30], X[31], X[16]);
endmodule

module undefined (
  input  CK,
  input  [31:0] instruction,
  output undefined
);

  wire add, addi, \and , and_1_out, and_2_out, and_3_out, and_4_out, and_5_out, and_6_out, and_7_out,
       and_8_out, and_9_out, beq, bne, j, lw, \nor , not_1_out, \or , or_1_out, slt, sub, sw, \xor ;

  and and_1 (and_1_out, ~instruction[26], ~instruction[27], ~instruction[28], ~instruction[29], ~instruction[30], ~instruction[31]);  // AND_Gate
  and and_2 (and_2_out, ~instruction[6], ~instruction[7], ~instruction[8], ~instruction[9], ~instruction[10]);  // AND_Gate
  and and_3 (and_3_out, ~instruction[0], ~instruction[1], ~instruction[2], ~instruction[3], ~instruction[4], instruction[5]);  // AND_Gate
  and and_4 (and_4_out, ~instruction[0], instruction[1], ~instruction[2], ~instruction[3], ~instruction[4], instruction[5]);  // AND_Gate
  and and_5 (and_5_out, ~instruction[0], ~instruction[1], instruction[2], ~instruction[3], ~instruction[4], instruction[5]);  // AND_Gate
  and and_6 (and_6_out, instruction[0], ~instruction[1], instruction[2], ~instruction[3], ~instruction[4], instruction[5]);  // AND_Gate
  and and_7 (and_7_out, ~instruction[0], instruction[1], instruction[2], ~instruction[3], ~instruction[4], instruction[5]);  // AND_Gate
  and and_8 (and_8_out, instruction[0], instruction[1], instruction[2], ~instruction[3], ~instruction[4], instruction[5]);  // AND_Gate
  and and_9 (and_9_out, ~instruction[0], instruction[1], ~instruction[2], instruction[3], ~instruction[4], instruction[5]);  // AND_Gate
  and and_10 (add, and_1_out, and_2_out, and_3_out);
  and and_11 (sub, and_1_out, and_2_out, and_4_out);
  and and_12 (\and , and_1_out, and_2_out, and_5_out);
  and and_13 (\or , and_1_out, and_2_out, and_6_out);
  and and_14 (\xor , and_1_out, and_2_out, and_7_out);
  and and_15 (\nor , and_1_out, and_2_out, and_8_out);
  and and_16 (slt, and_1_out, and_2_out, and_9_out);
  and and_17 (lw, instruction[26], instruction[27], ~instruction[28], ~instruction[29], ~instruction[30], instruction[31]);  // AND_Gate
  and and_18 (sw, instruction[26], instruction[27], ~instruction[28], instruction[29], ~instruction[30], instruction[31]);  // AND_Gate
  and and_19 (bne, instruction[26], ~instruction[27], instruction[28], ~instruction[29], ~instruction[30], ~instruction[31]);  // AND_Gate
  and and_20 (beq, ~instruction[26], ~instruction[27], instruction[28], ~instruction[29], ~instruction[30], ~instruction[31]);  // AND_Gate
  and and_21 (addi, ~instruction[26], ~instruction[27], ~instruction[28], instruction[29], ~instruction[30], ~instruction[31]);  // AND_Gate
  and and_22 (j, ~instruction[26], instruction[27], ~instruction[28], ~instruction[29], ~instruction[30], ~instruction[31]);  // AND_Gate
  or or_1 (or_1_out, add, sub, \and , \or , \xor , \nor , slt, lw, sw, bne, beq, addi, j);
  not not_1 (not_1_out, or_1_out);
  D_Flip_Flop d_ff_1 (.clk(CK), .D(not_1_out), .Q(undefined), .en(not_1_out));  // open: Qn, preset, reset
endmodule

module addr_error (
  input  CK,
  input  [31:0] addr,
  input  WE,
  input  RE,
  output addr_error
);

  wire and_1_out, and_2_out, comparator_1_lt, comparator_2_gt, or_1_out, or_2_out, or_3_out, or_4_out;

  Hex_Digit_Display hex_digit_display_1 (.value(addr[31:28]));  // open: dp
  Hex_Digit_Display hex_digit_display_2 (.value(addr[27:24]));  // open: dp
  Hex_Digit_Display hex_digit_display_3 (.value(addr[23:20]));  // open: dp
  Hex_Digit_Display hex_digit_display_4 (.value(addr[19:16]));  // open: dp
  Hex_Digit_Display hex_digit_display_5 (.value(addr[15:12]));  // open: dp
  Hex_Digit_Display hex_digit_display_6 (.value(addr[11:8]));  // open: dp
  or or_1 (or_1_out, WE, RE);
  Comparator #(.width(32), .mode("unsigned")) comparator_1 (
    .a(addr), .b(32'h1000), .lt(comparator_1_lt));  // open: gt, eq
  Comparator #(.width(32), .mode("unsigned")) comparator_2 (
    .a(addr), .b(32'h2ffc), .gt(comparator_2_gt));  // open: eq, lt
  Hex_Digit_Display hex_digit_display_7 (.value(addr[3:0]));  // open: dp
  Hex_Digit_Display hex_digit_display_8 (.value(addr[7:4]));  // open: dp
  or or_2 (or_2_out, addr[0], addr[1]);
  or or_3 (or_3_out, comparator_1_lt, comparator_2_gt);
  and and_1 (and_1_out, or_2_out, or_1_out);
  and and_2 (and_2_out, or_1_out, or_3_out);
  or or_4 (or_4_out, and_1_out, and_2_out);
  D_Flip_Flop d_ff_1 (.clk(CK), .D(or_4_out), .Q(addr_error), .en(or_4_out));  // open: Qn, preset, reset
endmodule

module disassemble (
  input  [31:0] instruction,
  output [6:0] n1,
  output [6:0] n2,
  output [6:0] n3,
  output [6:0] n4,
  output [3:0] r1h,
  output [3:0] r1l,
  output [3:0] r2h,
  output [3:0] r2l,
  output [3:0] r3h,
  output [3:0] r3l,
  output [3:0] i7,
  output [3:0] i6,
  output [3:0] i5,
  output [3:0] i4,
  output [3:0] i3,
  output [3:0] i2,
  output [3:0] i1
);

  wire disa1_1_add, disa1_1_addi, disa1_1_and, disa1_1_beq, disa1_1_bne, disa1_1_j, disa1_1_lw, disa1_1_nor,
       disa1_1_or, disa1_1_slt, disa1_1_sub, disa1_1_sw, disa1_1_xor;

  disa_op2 disa_op2_1 (.instruction(instruction), ._7(i7), ._6(i6), ._5(i5), ._4(i4), ._3(i3), ._2(i2), ._1(i1));
  disa1 disa1_1 (
    .instruction(instruction), .add(disa1_1_add), .sub(disa1_1_sub), .\and (disa1_1_and), .\or (disa1_1_or),
    .\xor (disa1_1_xor), .\nor (disa1_1_nor), .slt(disa1_1_slt), .lw(disa1_1_lw), .sw(disa1_1_sw),
    .bne(disa1_1_bne), .beq(disa1_1_beq), .addi(disa1_1_addi), .j(disa1_1_j));
  disa_op1 disa_op1_1 (
    .instruction(instruction), .operand1h(r1h), .operand1l(r1l), .operand2h(r2h), .operand2l(r2l),
    .operand3h(r3h), .operand3l(r3l));
  disa_n1 disa_n1_1 (
    .add(disa1_1_add), .sub(disa1_1_sub), .\and (disa1_1_and), .\or (disa1_1_or), .\xor (disa1_1_xor),
    .\nor (disa1_1_nor), .slt(disa1_1_slt), .lw(disa1_1_lw), .sw(disa1_1_sw), .bne(disa1_1_bne),
    .beq(disa1_1_beq), .addi(disa1_1_addi), .j(disa1_1_j), .out(n1));
  disa_n2 disa_n2_1 (
    .add(disa1_1_add), .sub(disa1_1_sub), .\and (disa1_1_and), .\or (disa1_1_or), .\xor (disa1_1_xor),
    .\nor (disa1_1_nor), .slt(disa1_1_slt), .lw(disa1_1_lw), .sw(disa1_1_sw), .bne(disa1_1_bne),
    .beq(disa1_1_beq), .addi(disa1_1_addi), .j(disa1_1_j), .out(n2));
  disa_n3 disa_n3_1 (
    .add(disa1_1_add), .sub(disa1_1_sub), .\and (disa1_1_and), .\or (disa1_1_or), .\xor (disa1_1_xor),
    .\nor (disa1_1_nor), .slt(disa1_1_slt), .lw(disa1_1_lw), .sw(disa1_1_sw), .bne(disa1_1_bne),
    .beq(disa1_1_beq), .addi(disa1_1_addi), .j(disa1_1_j), .out(n3));
  disa_n4 disa_n4_1 (
    .add(disa1_1_add), .sub(disa1_1_sub), .\and (disa1_1_and), .\or (disa1_1_or), .\xor (disa1_1_xor),
    .\nor (disa1_1_nor), .slt(disa1_1_slt), .lw(disa1_1_lw), .sw(disa1_1_sw), .bne(disa1_1_bne),
    .beq(disa1_1_beq), .addi(disa1_1_addi), .j(disa1_1_j), .out(n4));
  _7_Segment_Display u_7_segment_display_1 (
    .g(n1[6]), .f(n1[5]), .a(n1[4]), .b(n1[3]), .e(n1[2]), .d(n1[1]), .c(n1[0]));  // open: dp
  _7_Segment_Display u_7_segment_display_2 (
    .g(n2[6]), .f(n2[5]), .a(n2[4]), .b(n2[3]), .e(n2[2]), .d(n2[1]), .c(n2[0]));  // open: dp
  _7_Segment_Display u_7_segment_display_3 (
    .g(n3[6]), .f(n3[5]), .a(n3[4]), .b(n3[3]), .e(n3[2]), .d(n3[1]), .c(n3[0]));  // open: dp
  _7_Segment_Display u_7_segment_display_4 (
    .g(n4[6]), .f(n4[5]), .a(n4[4]), .b(n4[3]), .e(n4[2]), .d(n4[1]), .c(n4[0]));  // open: dp
  Hex_Digit_Display hex_digit_display_1 (.value(r1h));  // open: dp
  Hex_Digit_Display hex_digit_display_2 (.value(r1l));  // open: dp
  Hex_Digit_Display hex_digit_display_3 (.value(r2h));  // open: dp
  Hex_Digit_Display hex_digit_display_4 (.value(r2l));  // open: dp
  Hex_Digit_Display hex_digit_display_5 (.value(r3l));  // open: dp
  Hex_Digit_Display hex_digit_display_6 (.value(r3h));  // open: dp
  Hex_Digit_Display hex_digit_display_7 (.value(i7));  // open: dp
  Hex_Digit_Display hex_digit_display_8 (.value(i5));  // open: dp
  Hex_Digit_Display hex_digit_display_9 (.value(i6));  // open: dp
  Hex_Digit_Display hex_digit_display_10 (.value(i4));  // open: dp
  Hex_Digit_Display hex_digit_display_11 (.value(i3));  // open: dp
  Hex_Digit_Display hex_digit_display_12 (.value(i1));  // open: dp
  Hex_Digit_Display hex_digit_display_13 (.value(i2));  // open: dp
endmodule

module disa_n1 (
  input  add,
  input  sub,
  input  \and ,
  input  \or ,
  input  \xor ,
  input  \nor ,
  input  slt,
  input  lw,
  input  sw,
  input  bne,
  input  beq,
  input  addi,
  input  j,
  output [6:0] out
);

  wire [6:0] and_1_out, and_2_out, and_3_out, and_4_out, and_5_out, and_6_out, and_7_out, and_8_out,
       and_9_out, and_10_out, and_11_out, and_12_out, and_13_out;

  assign and_1_out = 7'b1111101 & {7{add}};  // AND_Gate and_1, 7 bits wide
  assign and_2_out = 7'b1100011 & {7{sub}};  // AND_Gate and_2, 7 bits wide
  assign and_3_out = 7'b1111101 & {7{\and }};  // AND_Gate and_3, 7 bits wide
  assign and_4_out = 7'b1000111 & {7{\or }};  // AND_Gate and_4, 7 bits wide
  assign and_5_out = 7'b1101101 & {7{\xor }};  // AND_Gate and_5, 7 bits wide
  assign and_6_out = 7'b1000101 & {7{\nor }};  // AND_Gate and_6, 7 bits wide
  assign and_7_out = 7'b0100110 & {7{lw}};  // AND_Gate and_7, 7 bits wide
  assign and_8_out = 7'b1100011 & {7{sw}};  // AND_Gate and_8, 7 bits wide
  assign and_9_out = 7'b1100111 & {7{bne}};  // AND_Gate and_9, 7 bits wide
  assign and_10_out = 7'b1100111 & {7{beq}};  // AND_Gate and_10, 7 bits wide
  assign and_11_out = 7'b1111101 & {7{addi}};  // AND_Gate and_11, 7 bits wide
  assign and_12_out = 7'b0001011 & {7{j}};  // AND_Gate and_12, 7 bits wide
  assign and_13_out = 7'b0001011 & {7{slt}};  // AND_Gate and_13, 7 bits wide
  assign out = and_1_out | and_2_out | and_3_out | and_4_out | and_5_out | and_6_out | and_7_out | and_8_out | and_9_out | and_10_out | and_11_out | and_12_out | and_13_out;  // OR_Gate or_1, 7 bits wide
  _7_Segment_Display u_7_segment_display_1 (
    .g(out[6]), .f(out[5]), .a(out[4]), .b(out[3]), .e(out[2]), .d(out[1]), .c(out[0]));  // open: dp
endmodule

module disa1 (
  input  [31:0] instruction,
  output add,
  output sub,
  output \and ,
  output \or ,
  output \xor ,
  output \nor ,
  output slt,
  output lw,
  output sw,
  output bne,
  output beq,
  output addi,
  output j
);

  wire and_1_out, and_2_out, and_3_out, and_4_out, and_5_out, and_6_out, and_7_out, and_8_out, and_9_out;

  and and_1 (and_1_out, ~instruction[26], ~instruction[27], ~instruction[28], ~instruction[29], ~instruction[30], ~instruction[31]);  // AND_Gate
  and and_2 (and_2_out, ~instruction[6], ~instruction[7], ~instruction[8], ~instruction[9], ~instruction[10]);  // AND_Gate
  and and_3 (and_3_out, ~instruction[0], ~instruction[1], ~instruction[2], ~instruction[3], ~instruction[4], instruction[5]);  // AND_Gate
  and and_4 (and_4_out, ~instruction[0], instruction[1], ~instruction[2], ~instruction[3], ~instruction[4], instruction[5]);  // AND_Gate
  and and_5 (and_5_out, ~instruction[0], ~instruction[1], instruction[2], ~instruction[3], ~instruction[4], instruction[5]);  // AND_Gate
  and and_6 (and_6_out, instruction[0], ~instruction[1], instruction[2], ~instruction[3], ~instruction[4], instruction[5]);  // AND_Gate
  and and_7 (and_7_out, ~instruction[0], instruction[1], instruction[2], ~instruction[3], ~instruction[4], instruction[5]);  // AND_Gate
  and and_8 (and_8_out, instruction[0], instruction[1], instruction[2], ~instruction[3], ~instruction[4], instruction[5]);  // AND_Gate
  and and_9 (and_9_out, ~instruction[0], instruction[1], ~instruction[2], instruction[3], ~instruction[4], instruction[5]);  // AND_Gate
  and and_10 (add, and_1_out, and_2_out, and_3_out);
  and and_11 (sub, and_1_out, and_2_out, and_4_out);
  and and_12 (\and , and_1_out, and_2_out, and_5_out);
  and and_13 (\or , and_1_out, and_2_out, and_6_out);
  and and_14 (\xor , and_1_out, and_2_out, and_7_out);
  and and_15 (\nor , and_1_out, and_2_out, and_8_out);
  and and_16 (slt, and_1_out, and_2_out, and_9_out);
  and and_17 (lw, instruction[26], instruction[27], ~instruction[28], ~instruction[29], ~instruction[30], instruction[31]);  // AND_Gate
  and and_18 (sw, instruction[26], instruction[27], ~instruction[28], instruction[29], ~instruction[30], instruction[31]);  // AND_Gate
  and and_19 (bne, instruction[26], ~instruction[27], instruction[28], ~instruction[29], ~instruction[30], ~instruction[31]);  // AND_Gate
  and and_20 (beq, ~instruction[26], ~instruction[27], instruction[28], ~instruction[29], ~instruction[30], ~instruction[31]);  // AND_Gate
  and and_21 (addi, ~instruction[26], ~instruction[27], ~instruction[28], instruction[29], ~instruction[30], ~instruction[31]);  // AND_Gate
  and and_22 (j, ~instruction[26], instruction[27], ~instruction[28], ~instruction[29], ~instruction[30], ~instruction[31]);  // AND_Gate
endmodule

module disa_n2 (
  input  add,
  input  sub,
  input  \and ,
  input  \or ,
  input  \xor ,
  input  \nor ,
  input  slt,
  input  lw,
  input  sw,
  input  bne,
  input  beq,
  input  addi,
  input  j,
  output [6:0] out
);

  wire [6:0] and_1_out, and_2_out, and_3_out, and_4_out, and_5_out, and_6_out, and_7_out, and_8_out,
       and_9_out, and_10_out, and_11_out, and_12_out, and_13_out;

  assign and_1_out = 7'b1001111 & {7{add}};  // AND_Gate and_1, 7 bits wide
  assign and_2_out = 7'b0000111 & {7{sub}};  // AND_Gate and_2, 7 bits wide
  assign and_3_out = 7'b1000101 & {7{\and }};  // AND_Gate and_3, 7 bits wide
  assign and_4_out = 7'b1000100 & {7{\or }};  // AND_Gate and_4, 7 bits wide
  assign and_5_out = 7'b1000111 & {7{\xor }};  // AND_Gate and_5, 7 bits wide
  assign and_6_out = 7'b1000111 & {7{\nor }};  // AND_Gate and_6, 7 bits wide
  assign and_7_out = 7'b1101111 & {7{lw}};  // AND_Gate and_7, 7 bits wide
  assign and_8_out = 7'b1101111 & {7{sw}};  // AND_Gate and_8, 7 bits wide
  assign and_9_out = 7'b1000101 & {7{bne}};  // AND_Gate and_9, 7 bits wide
  assign and_10_out = 7'b1110110 & {7{beq}};  // AND_Gate and_10, 7 bits wide
  assign and_11_out = 7'b1001111 & {7{addi}};  // AND_Gate and_11, 7 bits wide
  assign and_12_out = {7{1'b0}} & {7{j}};  // AND_Gate and_12, 7 bits wide
  assign and_13_out = 7'b0100110 & {7{slt}};  // AND_Gate and_13, 7 bits wide
  assign out = and_1_out | and_2_out | and_3_out | and_4_out | and_5_out | and_6_out | and_7_out | and_8_out | and_9_out | and_10_out | and_11_out | and_12_out | and_13_out;  // OR_Gate or_1, 7 bits wide
  _7_Segment_Display u_7_segment_display_1 (
    .g(out[6]), .f(out[5]), .a(out[4]), .b(out[3]), .e(out[2]), .d(out[1]), .c(out[0]));  // open: dp
endmodule

module disa_n3 (
  input  add,
  input  sub,
  input  \and ,
  input  \or ,
  input  \xor ,
  input  \nor ,
  input  slt,
  input  lw,
  input  sw,
  input  bne,
  input  beq,
  input  addi,
  input  j,
  output [6:0] out
);

  wire [6:0] and_1_out, and_2_out, and_3_out, and_4_out, and_5_out, and_6_out, and_7_out, and_8_out,
       and_9_out, and_10_out, and_11_out, and_12_out, and_13_out;

  assign and_1_out = 7'b1001111 & {7{add}};  // AND_Gate and_1, 7 bits wide
  assign and_2_out = 7'b1100111 & {7{sub}};  // AND_Gate and_2, 7 bits wide
  assign and_3_out = 7'b1001111 & {7{\and }};  // AND_Gate and_3, 7 bits wide
  assign and_4_out = {7{1'b0}} & {7{\or }};  // AND_Gate and_4, 7 bits wide
  assign and_5_out = 7'b1000100 & {7{\xor }};  // AND_Gate and_5, 7 bits wide
  assign and_6_out = 7'b1000100 & {7{\nor }};  // AND_Gate and_6, 7 bits wide
  assign and_7_out = {7{1'b0}} & {7{lw}};  // AND_Gate and_7, 7 bits wide
  assign and_8_out = {7{1'b0}} & {7{sw}};  // AND_Gate and_8, 7 bits wide
  assign and_9_out = 7'b1110110 & {7{bne}};  // AND_Gate and_9, 7 bits wide
  assign and_10_out = 7'b1111110 & {7{beq}};  // AND_Gate and_10, 7 bits wide
  assign and_11_out = 7'b1001111 & {7{addi}};  // AND_Gate and_11, 7 bits wide
  assign and_12_out = {7{1'b0}} & {7{j}};  // AND_Gate and_12, 7 bits wide
  assign and_13_out = 7'b1100110 & {7{slt}};  // AND_Gate and_13, 7 bits wide
  assign out = and_1_out | and_2_out | and_3_out | and_4_out | and_5_out | and_6_out | and_7_out | and_8_out | and_9_out | and_10_out | and_11_out | and_12_out | and_13_out;  // OR_Gate or_1, 7 bits wide
  _7_Segment_Display u_7_segment_display_1 (
    .g(out[6]), .f(out[5]), .a(out[4]), .b(out[3]), .e(out[2]), .d(out[1]), .c(out[0]));  // open: dp
endmodule

module disa_n4 (
  input  add,
  input  sub,
  input  \and ,
  input  \or ,
  input  \xor ,
  input  \nor ,
  input  slt,
  input  lw,
  input  sw,
  input  bne,
  input  beq,
  input  addi,
  input  j,
  output [6:0] out
);

  wire [6:0] and_1_out, and_2_out, and_3_out, and_4_out, and_5_out, and_6_out, and_7_out, and_8_out,
       and_9_out, and_10_out, and_11_out, and_12_out, and_13_out;

  assign and_1_out = {7{1'b0}} & {7{add}};  // AND_Gate and_1, 7 bits wide
  assign and_2_out = {7{1'b0}} & {7{sub}};  // AND_Gate and_2, 7 bits wide
  assign and_3_out = {7{1'b0}} & {7{\and }};  // AND_Gate and_3, 7 bits wide
  assign and_4_out = {7{1'b0}} & {7{\or }};  // AND_Gate and_4, 7 bits wide
  assign and_5_out = {7{1'b0}} & {7{\xor }};  // AND_Gate and_5, 7 bits wide
  assign and_6_out = {7{1'b0}} & {7{\nor }};  // AND_Gate and_6, 7 bits wide
  assign and_7_out = {7{1'b0}} & {7{lw}};  // AND_Gate and_7, 7 bits wide
  assign and_8_out = {7{1'b0}} & {7{sw}};  // AND_Gate and_8, 7 bits wide
  assign and_9_out = {7{1'b0}} & {7{bne}};  // AND_Gate and_9, 7 bits wide
  assign and_10_out = {7{1'b0}} & {7{beq}};  // AND_Gate and_10, 7 bits wide
  assign and_11_out = 7'b0000001 & {7{addi}};  // AND_Gate and_11, 7 bits wide
  assign and_12_out = {7{1'b0}} & {7{j}};  // AND_Gate and_12, 7 bits wide
  assign and_13_out = {7{1'b0}} & {7{slt}};  // AND_Gate and_13, 7 bits wide
  assign out = and_1_out | and_2_out | and_3_out | and_4_out | and_5_out | and_6_out | and_7_out | and_8_out | and_9_out | and_10_out | and_11_out | and_12_out | and_13_out;  // OR_Gate or_1, 7 bits wide
  _7_Segment_Display u_7_segment_display_1 (
    .g(out[6]), .f(out[5]), .a(out[4]), .b(out[3]), .e(out[2]), .d(out[1]), .c(out[0]));  // open: dp
endmodule

module disa_op1 (
  input  [31:0] instruction,
  output [3:0] operand1h,
  output [3:0] operand1l,
  output [3:0] operand2h,
  output [3:0] operand2l,
  output [3:0] operand3h,
  output [3:0] operand3l
);

  wire add, addi, \and , beq, bne, j, lw, \nor , \or , or_4_out, slt, sub, sw, \xor ;
  wire [3:0] and_1_out, and_2_out, and_3_out, and_4_out, and_5_out, and_6_out, and_7_out, and_8_out,
       and_9_out, and_10_out, and_11_out, and_12_out, or_3_out, or_5_out, or_6_out, or_7_out, or_8_out,
       or_9_out;
  wire [3:3] or_1_out, or_2_out;

  disa1 disa1_1 (
    .instruction(instruction), .add(add), .sub(sub), .\and (\and ), .\or (\or ), .\xor (\xor ),
    .\nor (\nor ), .slt(slt), .lw(lw), .sw(sw), .bne(bne), .beq(beq), .addi(addi), .j(j));
  or or_1 (or_1_out[3], add, sub, \and , \or , \xor , \nor , slt);
  or or_2 (or_2_out[3], lw, sw, bne, beq, addi);
  assign and_1_out = {3'b000, instruction[15]} & {4{or_1_out[3]}};  // AND_Gate and_1, 4 bits wide
  assign and_2_out = {3'b000, instruction[20]} & {4{or_2_out[3]}};  // AND_Gate and_2, 4 bits wide
  assign and_3_out = instruction[14:11] & {4{or_1_out[3]}};  // AND_Gate and_3, 4 bits wide
  assign and_4_out = instruction[19:16] & {4{or_2_out[3]}};  // AND_Gate and_4, 4 bits wide
  assign and_5_out = {3'b000, instruction[25]} & {4{or_1_out[3]}};  // AND_Gate and_5, 4 bits wide
  assign and_6_out = {3'b000, instruction[25]} & {4{or_2_out[3]}};  // AND_Gate and_6, 4 bits wide
  assign and_7_out = instruction[24:21] & {4{or_1_out[3]}};  // AND_Gate and_7, 4 bits wide
  assign and_8_out = instruction[24:21] & {4{or_2_out[3]}};  // AND_Gate and_8, 4 bits wide
  assign and_9_out = {3'b000, instruction[20]} & {4{or_1_out[3]}};  // AND_Gate and_9, 4 bits wide
  assign and_10_out = instruction[24:21] & {4{or_2_out[3]}};  // AND_Gate and_10, 4 bits wide
  assign and_11_out = instruction[19:16] & {4{or_1_out[3]}};  // AND_Gate and_11, 4 bits wide
  assign and_12_out = instruction[24:21] & {4{or_2_out[3]}};  // AND_Gate and_12, 4 bits wide
  assign operand1h = or_4_out ? or_3_out : 4'bz;  // Controlled_Buffer controlled_buffer_1
  assign or_3_out = and_1_out | and_2_out;  // OR_Gate or_3, 4 bits wide
  or or_4 (or_4_out, or_1_out[3], or_2_out[3]);
  assign or_5_out = and_3_out | and_4_out;  // OR_Gate or_5, 4 bits wide
  assign operand1l = or_4_out ? or_5_out : 4'bz;  // Controlled_Buffer controlled_buffer_2
  assign operand2h = or_4_out ? or_6_out : 4'bz;  // Controlled_Buffer controlled_buffer_3
  assign or_6_out = and_5_out | and_6_out;  // OR_Gate or_6, 4 bits wide
  assign or_7_out = and_7_out | and_8_out;  // OR_Gate or_7, 4 bits wide
  assign operand2l = or_4_out ? or_7_out : 4'bz;  // Controlled_Buffer controlled_buffer_4
  assign operand3h = or_1_out[3] ? or_8_out : 4'bz;  // Controlled_Buffer controlled_buffer_5
  assign or_8_out = and_9_out | and_10_out;  // OR_Gate or_8, 4 bits wide
  assign or_9_out = and_11_out | and_12_out;  // OR_Gate or_9, 4 bits wide
  assign operand3l = or_1_out[3] ? or_9_out : 4'bz;  // Controlled_Buffer controlled_buffer_6
  Hex_Digit_Display hex_digit_display_1 (.value(operand1h));  // open: dp
  Hex_Digit_Display hex_digit_display_2 (.value(operand1l));  // open: dp
  Hex_Digit_Display hex_digit_display_3 (.value(operand2h));  // open: dp
  Hex_Digit_Display hex_digit_display_4 (.value(operand2l));  // open: dp
  Hex_Digit_Display hex_digit_display_5 (.value(operand3l));  // open: dp
  Hex_Digit_Display hex_digit_display_6 (.value(operand3h));  // open: dp
endmodule

module disa_op2 (
  input  [31:0] instruction,
  output [3:0] _7,
  output [3:0] _6,
  output [3:0] _5,
  output [3:0] _4,
  output [3:0] _3,
  output [3:0] _2,
  output [3:0] _1
);

  wire add, addi, \and , beq, bne, j, lw, \nor , \or , slt, sub, sw, \xor ;
  wire [3:0] and_1_out, and_2_out, and_3_out, and_4_out, and_5_out, and_6_out, and_7_out, or_1_out, or_3_out,
       or_5_out, or_7_out;
  wire [3:3] or_2_out, or_4_out, or_6_out, or_8_out;

  disa1 disa1_1 (
    .instruction(instruction), .add(add), .sub(sub), .\and (\and ), .\or (\or ), .\xor (\xor ),
    .\nor (\nor ), .slt(slt), .lw(lw), .sw(sw), .bne(bne), .beq(beq), .addi(addi), .j(j));
  assign or_1_out = {4{j}} | {4{or_2_out[3]}};  // OR_Gate or_1, 4 bits wide
  or or_2 (or_2_out[3], lw, sw, bne, beq, addi);
  assign or_3_out = {4{j}} | {4{or_4_out[3]}};  // OR_Gate or_3, 4 bits wide
  or or_4 (or_4_out[3], lw, sw, bne, beq, addi);
  assign or_5_out = {4{j}} | {4{or_6_out[3]}};  // OR_Gate or_5, 4 bits wide
  or or_6 (or_6_out[3], lw, sw, bne, beq, addi);
  assign or_7_out = {4{j}} | {4{or_8_out[3]}};  // OR_Gate or_7, 4 bits wide
  or or_8 (or_8_out[3], lw, sw, bne, beq, addi);
  assign and_1_out = {2'b00, instruction[25:24]} & {4{j}};  // AND_Gate and_1, 4 bits wide
  assign and_2_out = instruction[23:20] & {4{j}};  // AND_Gate and_2, 4 bits wide
  assign and_3_out = instruction[19:16] & {4{j}};  // AND_Gate and_3, 4 bits wide
  assign and_4_out = instruction[15:12] & or_1_out;  // AND_Gate and_4, 4 bits wide
  assign and_5_out = instruction[11:8] & or_3_out;  // AND_Gate and_5, 4 bits wide
  assign and_6_out = instruction[7:4] & or_5_out;  // AND_Gate and_6, 4 bits wide
  assign and_7_out = instruction[3:0] & or_7_out;  // AND_Gate and_7, 4 bits wide
  assign _7 = j ? and_1_out : 4'bz;  // Controlled_Buffer controlled_buffer_1
  assign _6 = j ? and_2_out : 4'bz;  // Controlled_Buffer controlled_buffer_2
  assign _5 = j ? and_3_out : 4'bz;  // Controlled_Buffer controlled_buffer_3
  assign _4 = or_1_out[0] ? and_4_out : 4'bz;  // Controlled_Buffer controlled_buffer_4
  assign _3 = or_3_out[0] ? and_5_out : 4'bz;  // Controlled_Buffer controlled_buffer_5
  assign _2 = or_5_out[0] ? and_6_out : 4'bz;  // Controlled_Buffer controlled_buffer_6
  assign _1 = or_7_out[0] ? and_7_out : 4'bz;  // Controlled_Buffer controlled_buffer_7
  Hex_Digit_Display hex_digit_display_1 (.value(_7));  // open: dp
  Hex_Digit_Display hex_digit_display_2 (.value(_6));  // open: dp
  Hex_Digit_Display hex_digit_display_3 (.value(_5));  // open: dp
  Hex_Digit_Display hex_digit_display_4 (.value(_4));  // open: dp
  Hex_Digit_Display hex_digit_display_5 (.value(_3));  // open: dp
  Hex_Digit_Display hex_digit_display_6 (.value(_2));  // open: dp
  Hex_Digit_Display hex_digit_display_7 (.value(_1));  // open: dp
endmodule

module branch_sel (
  input  Branch,
  input  NZ,
  input  [31:0] instruction,
  output Branch_EX
);

  wire and_1_out, and_2_out, and_3_out, and_4_out, not_1_out;

  not not_1 (not_1_out, NZ);
  and and_1 (and_1_out, ~instruction[26], ~instruction[27], instruction[28], ~instruction[29], ~instruction[30], ~instruction[31]);  // AND_Gate
  and and_2 (and_2_out, instruction[26], ~instruction[27], instruction[28], ~instruction[29], ~instruction[30], ~instruction[31]);  // AND_Gate
  and and_3 (and_3_out, Branch, not_1_out, and_1_out);
  and and_4 (and_4_out, Branch, NZ, and_2_out);
  or or_1 (Branch_EX, and_3_out, and_4_out);

  // Notes on the sheet:
  //   beq
  //   bne
endmodule

module left2b (
  input  [31:0] In,
  output [31:0] Out
);

  Shifter #(.width(32)) shifter_1 (.in(In), .\dist (5'b00010), .out(Out));
endmodule

module mips (
);

  wire addr_error_1_addr_error, alu32_2_1_nz, ALUSrc, Branch, branch_sel_1_branch_ex, CK, Jump, MemRead,
       MemtoReg, MemWrite, not_1_out, RegDst, RegWrite, undefined_1_undefined;
  wire [1:0] mainc_2_1_aluop;
  wire [3:0] disassemble_1_i1, disassemble_1_i2, disassemble_1_i3, disassemble_1_i4, disassemble_1_i5,
       disassemble_1_i6, disassemble_1_i7, disassemble_1_r1h, disassemble_1_r1l, disassemble_1_r2h,
       disassemble_1_r2l, disassemble_1_r3h, disassemble_1_r3l;
  wire [4:0] aluc_2_1_alufunc, multiplexer_1_out;
  wire [6:0] disassemble_1_n1, disassemble_1_n2, disassemble_1_n3, disassemble_1_n4;
  wire [31:0] adder_1_out, adder_2_out, ALUA, ALUB, ALUX, bit_extender_1_out, Instruction, left2b_1_out,
       multiplexer_3_out, NextPC, PC, ram_1_data, reg32_1_rdata2, WD_Reg;

  Hex_Digit_Display hex_digit_display_1 (.value(PC[31:28]));  // open: dp
  Hex_Digit_Display hex_digit_display_2 (.value(NextPC[31:28]));  // open: dp
  Hex_Digit_Display hex_digit_display_3 (.value(Instruction[31:28]));  // open: dp
  undefined undefined_1 (.CK(CK), .instruction(Instruction), .undefined(undefined_1_undefined));
  Clock u_CK (.out(CK));
  Hex_Digit_Display hex_digit_display_4 (.value(PC[27:24]));  // open: dp
  Hex_Digit_Display hex_digit_display_5 (.value(PC[23:20]));  // open: dp
  Hex_Digit_Display hex_digit_display_6 (.value(NextPC[23:20]));  // open: dp
  Hex_Digit_Display hex_digit_display_7 (.value(NextPC[27:24]));  // open: dp
  Hex_Digit_Display hex_digit_display_8 (.value(Instruction[23:20]));  // open: dp
  Hex_Digit_Display hex_digit_display_9 (.value(Instruction[27:24]));  // open: dp
  addr_error addr_error_1 (.CK(CK), .addr(ALUX), .WE(MemWrite), .RE(MemRead), .addr_error(addr_error_1_addr_error));
  LED led_1 (.in(addr_error_1_addr_error));
  LED led_2 (.in(undefined_1_undefined));
  Register #(.width(32)) register_1 (.D(NextPC), .en(1'b1), .Q(PC), .clk(CK), .clr(1'b0));
  Hex_Digit_Display hex_digit_display_10 (.value(PC[15:12]));  // open: dp
  Hex_Digit_Display hex_digit_display_11 (.value(PC[19:16]));  // open: dp
  Hex_Digit_Display hex_digit_display_12 (.value(NextPC[19:16]));  // open: dp
  Hex_Digit_Display hex_digit_display_13 (.value(NextPC[15:12]));  // open: dp
  Hex_Digit_Display hex_digit_display_14 (.value(Instruction[19:16]));  // open: dp
  Hex_Digit_Display hex_digit_display_15 (.value(Instruction[15:12]));  // open: dp
  disassemble disassemble_1 (
    .instruction(Instruction), .n1(disassemble_1_n1), .n2(disassemble_1_n2), .n3(disassemble_1_n3),
    .n4(disassemble_1_n4), .r1h(disassemble_1_r1h), .r1l(disassemble_1_r1l), .r2h(disassemble_1_r2h),
    .r2l(disassemble_1_r2l), .r3h(disassemble_1_r3h), .r3l(disassemble_1_r3l), .i7(disassemble_1_i7),
    .i6(disassemble_1_i6), .i5(disassemble_1_i5), .i4(disassemble_1_i4), .i3(disassemble_1_i3),
    .i2(disassemble_1_i2), .i1(disassemble_1_i1));
  Adder #(.width(32)) adder_1 (.a(PC), .b(32'h4), .out(adder_1_out), .cin(1'b0));  // open: cout
  Hex_Digit_Display hex_digit_display_16 (.value(PC[11:8]));  // open: dp
  Hex_Digit_Display hex_digit_display_17 (.value(PC[7:4]));  // open: dp
  Hex_Digit_Display hex_digit_display_18 (.value(NextPC[7:4]));  // open: dp
  Hex_Digit_Display hex_digit_display_19 (.value(NextPC[11:8]));  // open: dp
  Hex_Digit_Display hex_digit_display_20 (.value(Instruction[7:4]));  // open: dp
  Hex_Digit_Display hex_digit_display_21 (.value(Instruction[11:8]));  // open: dp
  Hex_Digit_Display hex_digit_display_22 (.value(PC[3:0]));  // open: dp
  Hex_Digit_Display hex_digit_display_23 (.value(NextPC[3:0]));  // open: dp
  Hex_Digit_Display hex_digit_display_24 (.value(Instruction[3:0]));  // open: dp
  ROM #(.addrWidth(24), .dataWidth(32)) rom_1 (.addr(PC[25:2]), .data(Instruction));  // open: sel
  mainc_2 mainc_2_1 (
    .Op(Instruction[31:26]), .Jump(Jump), .Branch(Branch), .ALUSrc(ALUSrc), .MemRead(MemRead),
    .MemWrite(MemWrite), .MemtoRead(MemtoReg), .RegDst(RegDst), .RegWrite(RegWrite), .ALUOp(mainc_2_1_aluop));
  Multiplexer #(.width(5), .disabled(0), .enable("false")) multiplexer_1 (
    .in0(Instruction[20:16]), .in1(Instruction[15:11]), .out(multiplexer_1_out), .sel(RegDst));
  _7_Segment_Display u_7_segment_display_1 (
    .g(disassemble_1_n1[6]), .f(disassemble_1_n1[5]), .a(disassemble_1_n1[4]), .b(disassemble_1_n1[3]),
    .e(disassemble_1_n1[2]), .d(disassemble_1_n1[1]), .c(disassemble_1_n1[0]));  // open: dp
  aluc_2 aluc_2_1 (.Func(Instruction[5:0]), .ALUOp(mainc_2_1_aluop), .ALUfunc(aluc_2_1_alufunc));
  Reg32 reg32_1 (
    .RegWrite(RegWrite), .WP(multiplexer_1_out), .CK(CK), .Data(WD_Reg), .RP1(Instruction[25:21]),
    .RP2(Instruction[20:16]), .RDATA1(ALUA), .RDATA2(reg32_1_rdata2));
  assign bit_extender_1_out = {{16{Instruction[15]}}, Instruction[15:0]};  // Bit_Extender bit_extender_1
  _7_Segment_Display u_7_segment_display_2 (
    .g(disassemble_1_n2[6]), .f(disassemble_1_n2[5]), .a(disassemble_1_n2[4]), .b(disassemble_1_n2[3]),
    .e(disassemble_1_n2[2]), .d(disassemble_1_n2[1]), .c(disassemble_1_n2[0]));  // open: dp
  left2b left2b_1 (.In(bit_extender_1_out), .Out(left2b_1_out));
  Multiplexer #(.width(32), .disabled(0), .enable("false")) multiplexer_2 (
    .in0(reg32_1_rdata2), .in1(bit_extender_1_out), .out(ALUB), .sel(ALUSrc));
  _7_Segment_Display u_7_segment_display_3 (
    .g(disassemble_1_n3[6]), .f(disassemble_1_n3[5]), .a(disassemble_1_n3[4]), .b(disassemble_1_n3[3]),
    .e(disassemble_1_n3[2]), .d(disassemble_1_n3[1]), .c(disassemble_1_n3[0]));  // open: dp
  Adder #(.width(32)) adder_2 (.a(adder_1_out), .b(left2b_1_out), .out(adder_2_out));  // open: cin, cout
  _7_Segment_Display u_7_segment_display_4 (
    .g(disassemble_1_n4[6]), .f(disassemble_1_n4[5]), .a(disassemble_1_n4[4]), .b(disassemble_1_n4[3]),
    .e(disassemble_1_n4[2]), .d(disassemble_1_n4[1]), .c(disassemble_1_n4[0]));  // open: dp
  alu32_2 alu32_2_1 (
    .Cin(aluc_2_1_alufunc[2]), .B(ALUB), .A(ALUA), .S(aluc_2_1_alufunc), .X(ALUX), .NZ(alu32_2_1_nz));  // open: Cout
  Multiplexer #(.width(32), .disabled(0), .enable("false")) multiplexer_3 (
    .in0(adder_1_out), .in1(adder_2_out), .out(multiplexer_3_out), .sel(branch_sel_1_branch_ex));
  Hex_Digit_Display hex_digit_display_25 (.value(disassemble_1_r1h));  // open: dp
  Hex_Digit_Display hex_digit_display_26 (.value(disassemble_1_r1l));  // open: dp
  Multiplexer #(.width(32), .disabled(0), .enable("false")) multiplexer_4 (
    .in0(multiplexer_3_out), .in1({adder_1_out[31:28], Instruction[25:0], 2'b00}), .out(NextPC), .sel(Jump));
  branch_sel branch_sel_1 (
    .Branch(Branch), .NZ(alu32_2_1_nz), .instruction(Instruction), .Branch_EX(branch_sel_1_branch_ex));
  LED led_3 (.in(branch_sel_1_branch_ex));
  not not_1 (not_1_out, 1'b1);
  Hex_Digit_Display hex_digit_display_27 (.value(disassemble_1_r2h));  // open: dp
  LED led_4 (.in(Jump));
  RAM #(.addrWidth(24), .dataWidth(32), .bus("separate")) ram_1 (
    .addr(ALUX[25:2]), .din(reg32_1_rdata2), .data(ram_1_data), .str(MemWrite), .sel(1'b1), .clk(CK),
    .ld(MemRead), .clr(not_1_out));
  Hex_Digit_Display hex_digit_display_28 (.value(disassemble_1_r2l));  // open: dp
  Multiplexer #(.width(32), .disabled(0), .enable("false")) multiplexer_5 (
    .in0(ALUX), .in1(ram_1_data), .out(WD_Reg), .sel(MemtoReg));
  Hex_Digit_Display hex_digit_display_29 (.value(disassemble_1_r3h));  // open: dp
  Hex_Digit_Display hex_digit_display_30 (.value(disassemble_1_r3l));  // open: dp
  Hex_Digit_Display hex_digit_display_31 (.value(ALUA[31:28]));  // open: dp
  Hex_Digit_Display hex_digit_display_32 (.value(ALUA[27:24]));  // open: dp
  Hex_Digit_Display hex_digit_display_33 (.value(ALUB[31:28]));  // open: dp
  Hex_Digit_Display hex_digit_display_34 (.value(ALUB[27:24]));  // open: dp
  Hex_Digit_Display hex_digit_display_35 (.value(ALUX[31:28]));  // open: dp
  Hex_Digit_Display hex_digit_display_36 (.value(ALUX[27:24]));  // open: dp
  Hex_Digit_Display hex_digit_display_37 (.value(disassemble_1_i7));  // open: dp
  Hex_Digit_Display hex_digit_display_38 (.value(ALUA[23:20]));  // open: dp
  Hex_Digit_Display hex_digit_display_39 (.value(ALUA[19:16]));  // open: dp
  Hex_Digit_Display hex_digit_display_40 (.value(ALUB[23:20]));  // open: dp
  Hex_Digit_Display hex_digit_display_41 (.value(ALUB[19:16]));  // open: dp
  Hex_Digit_Display hex_digit_display_42 (.value(ALUX[23:20]));  // open: dp
  Hex_Digit_Display hex_digit_display_43 (.value(ALUX[19:16]));  // open: dp
  Hex_Digit_Display hex_digit_display_44 (.value(disassemble_1_i5));  // open: dp
  Hex_Digit_Display hex_digit_display_45 (.value(disassemble_1_i6));  // open: dp
  Hex_Digit_Display hex_digit_display_46 (.value(ALUA[15:12]));  // open: dp
  Hex_Digit_Display hex_digit_display_47 (.value(ALUA[11:8]));  // open: dp
  Hex_Digit_Display hex_digit_display_48 (.value(ALUB[11:8]));  // open: dp
  Hex_Digit_Display hex_digit_display_49 (.value(ALUB[15:12]));  // open: dp
  Hex_Digit_Display hex_digit_display_50 (.value(ALUX[11:8]));  // open: dp
  Hex_Digit_Display hex_digit_display_51 (.value(ALUX[15:12]));  // open: dp
  Hex_Digit_Display hex_digit_display_52 (.value(disassemble_1_i3));  // open: dp
  Hex_Digit_Display hex_digit_display_53 (.value(disassemble_1_i4));  // open: dp
  Hex_Digit_Display hex_digit_display_54 (.value(ALUA[3:0]));  // open: dp
  Hex_Digit_Display hex_digit_display_55 (.value(ALUA[7:4]));  // open: dp
  Hex_Digit_Display hex_digit_display_56 (.value(ALUB[7:4]));  // open: dp
  Hex_Digit_Display hex_digit_display_57 (.value(ALUB[3:0]));  // open: dp
  Hex_Digit_Display hex_digit_display_58 (.value(ALUX[7:4]));  // open: dp
  Hex_Digit_Display hex_digit_display_59 (.value(ALUX[3:0]));  // open: dp
  Hex_Digit_Display hex_digit_display_60 (.value(disassemble_1_i2));  // open: dp
  Hex_Digit_Display hex_digit_display_61 (.value(disassemble_1_i1));  // open: dp
  Hex_Digit_Display hex_digit_display_62 (.value(WD_Reg[31:28]));  // open: dp
  Hex_Digit_Display hex_digit_display_63 (.value(WD_Reg[27:24]));  // open: dp
  Hex_Digit_Display hex_digit_display_64 (.value(WD_Reg[19:16]));  // open: dp
  Hex_Digit_Display hex_digit_display_65 (.value(WD_Reg[23:20]));  // open: dp
  Hex_Digit_Display hex_digit_display_66 (.value(WD_Reg[15:12]));  // open: dp
  Hex_Digit_Display hex_digit_display_67 (.value(WD_Reg[11:8]));  // open: dp
  Hex_Digit_Display hex_digit_display_68 (.value(WD_Reg[3:0]));  // open: dp
  Hex_Digit_Display hex_digit_display_69 (.value(WD_Reg[7:4]));  // open: dp

  // Notes on the sheet:
  //   データメモリアドレスエラー
  //   未定義命令の実行エラー
  //   現在のPCの値
  //   次のPCの値
  //   命令の機械語コード
  //   contents of rom_1 (hex, n*v repeats v):
  //   20130001 20120001 20100001 2016001f 22100001 2516820 22510000 21b20000 1616fffb 2517020 ac0d2040
  //   ac0e2044 1000ffff
  //   Branch Enable
  //   命令内のレジスタ番号(16進)
  //   ALUのA入力の値
  //   ALUのB入力の値
  //   ALUの出力の値
  //   即値(16進)
  //   レジスタへの書き込みデータ
endmodule
