// Logisim project report2021.circ as structural Verilog
module nsl (
  input  Q1,
  input  Q1B,
  input  Q2,
  input  Q2B,
  input  X1,
  input  X1B,
  input  X2,
  input  X2B,
  output D1,
  output D2
);

  wire nand_1_out, nand_2_out, nand_3_out, nand_4_out, nand_5_out;

  nand nand_1 (nand_1_out, Q1B, Q2, X2);
  nand nand_2 (nand_2_out, Q1, X1B, X2B);
  nand nand_3 (nand_3_out, Q1, Q2B, X2);
  nand nand_4 (nand_4_out, Q2, X1B, X2B);
  nand nand_5 (nand_5_out, Q2B, X2);
  nand nand_6 (D1, nand_1_out, nand_2_out, nand_3_out);
  nand nand_7 (D2, nand_4_out, nand_5_out);
endmodule

module outl (
  input  Q1,
  input  Q1B,
  input  Q2,
  input  Q2B,
  input  X1,
  input  X1B,
  input  X2,
  input  X2B,
  output Z1,
  output Z2,
  output Z3,
  output Z4
);

  wire nand_1_out, nand_2_out, nand_3_out, nand_4_out, nand_5_out;

  nand nand_1 (nand_1_out, Q1, Q2, X2);
  nand nand_2 (nand_2_out, Q1, Q2, X1);
  nand nand_3 (nand_3_out, Q1B, Q2, X1);
  nand nand_4 (nand_4_out, Q1, Q2B, X1);
  nand nand_5 (nand_5_out, Q2B, X1);
  not not_1 (Z2, nand_2_out);
  not not_2 (Z4, nand_5_out);
  nand nand_6 (Z1, nand_1_out, X1B);
  nand nand_7 (Z3, nand_3_out, nand_4_out);
endmodule

module vendor_seq (
  input  CK,
  input  RESET,
  input  X1,
  input  X2,
  output D1,
  output D2,
  output Z1,
  output Z2,
  output Z3,
  output Z4
);

  wire d_ff_1_q, d_ff_1_qn, d_ff_2_q, d_ff_2_qn, not_1_out, not_2_out;

  D_Flip_Flop d_ff_1 (.clk(CK), .D(D1), .Q(d_ff_1_q), .Qn(d_ff_1_qn), .preset(1'b0), .reset(RESET));  // open: en
  D_Flip_Flop d_ff_2 (.clk(CK), .D(D2), .Q(d_ff_2_q), .Qn(d_ff_2_qn), .preset(1'b0), .reset(RESET));  // open: en
  not not_1 (not_1_out, X1);
  not not_2 (not_2_out, X2);
  nsl nsl_1 (
    .Q1(d_ff_1_q), .Q1B(d_ff_1_qn), .Q2(d_ff_2_q), .Q2B(d_ff_2_qn), .X1(X1), .X1B(not_1_out), .X2(X2),
    .X2B(not_2_out), .D1(D1), .D2(D2));
  outl outl_1 (
    .Q1(d_ff_1_q), .Q1B(d_ff_1_qn), .Q2(d_ff_2_q), .Q2B(d_ff_2_qn), .X1(X1), .X1B(not_1_out), .X2(X2),
    .X2B(not_2_out), .Z1(Z1), .Z2(Z2), .Z3(Z3), .Z4(Z4));
endmodule

module test_vendor (
);

  wire CK, comparator_1_eq, comparator_2_eq, d_ff_1_q, not_1_out;
  wire [5:0] vendor_seq_1_z4;
  wire [7:0] adder_1_out, counter_1_q, counter_2_q;
  wire [8:0] rom_1_data;

  Clock u_CK (.out(CK));
  Hex_Digit_Display hex_digit_display_1 (.value(counter_1_q[7:4]));  // open: dp
  Counter counter_1 (.D(adder_1_out), .Q(counter_1_q), .clk(CK), .clr(comparator_1_eq));  // open: load, count, carry
  Hex_Digit_Display hex_digit_display_2 (.value(counter_1_q[3:0]));  // open: dp
  Adder adder_1 (.a(8'h1), .b(counter_1_q), .out(adder_1_out));  // open: cin, cout
  Comparator comparator_1 (.a(adder_1_out), .b(8'h14), .eq(comparator_1_eq));  // open: gt, lt
  ROM #(.dataWidth(9)) rom_1 (.addr(counter_1_q), .data(rom_1_data));  // open: sel
  Hex_Digit_Display hex_digit_display_3 (.value({3'b000, rom_1_data[8]}));  // open: dp
  Hex_Digit_Display hex_digit_display_4 (.value(rom_1_data[3:0]));  // open: dp
  Hex_Digit_Display hex_digit_display_5 (.value(rom_1_data[7:4]));  // open: dp
  vendor_seq vendor_seq_1 (
    .CK(CK), .RESET(rom_1_data[8]), .X1(rom_1_data[7]), .X2(rom_1_data[6]), .D1(vendor_seq_1_z4[5]),
    .D2(vendor_seq_1_z4[4]), .Z1(vendor_seq_1_z4[3]), .Z2(vendor_seq_1_z4[2]), .Z3(vendor_seq_1_z4[1]),
    .Z4(vendor_seq_1_z4[0]));
  DotMatrix #(.matrixcols(2), .matrixrows(1)) dotmatrix_1 (.col0(vendor_seq_1_z4[5]), .col1(vendor_seq_1_z4[4]));
  DotMatrix #(.matrixcols(4), .matrixrows(1)) dotmatrix_2 (
    .col0(vendor_seq_1_z4[3]), .col1(vendor_seq_1_z4[2]), .col2(vendor_seq_1_z4[1]), .col3(vendor_seq_1_z4[0]));
  DotMatrix #(.matrixcols(2), .matrixrows(1)) dotmatrix_3 (.col0(rom_1_data[5]), .col1(rom_1_data[4]));
  Comparator #(.width(6)) comparator_2 (
    .a(vendor_seq_1_z4), .b(rom_1_data[5:0]), .eq(comparator_2_eq));  // open: gt, lt
  LED led_1 (.in(comparator_2_eq));
  DotMatrix #(.matrixcols(4), .matrixrows(1)) dotmatrix_4 (
    .col0(rom_1_data[3]), .col1(rom_1_data[2]), .col2(rom_1_data[1]), .col3(rom_1_data[0]));
  Counter counter_2 (
    .D({8{1'b0}}), .count(not_1_out), .Q(counter_2_q), .clk(CK), .clr(comparator_1_eq));  // open: load, carry
  not not_1 (not_1_out, comparator_2_eq);
  Hex_Digit_Display hex_digit_display_6 (.value(counter_2_q[7:4]));  // open: dp
  D_Flip_Flop d_ff_1 (.clk(CK), .D(not_1_out), .Q(d_ff_1_q), .en(not_1_out));  // open: Qn, preset, reset
  Hex_Digit_Display hex_digit_display_7 (.value(counter_2_q[3:0]));  // open: dp
  LED led_2 (.in(d_ff_1_q));

  // Notes on the sheet:
  //   contents of rom_1 (hex, n*v repeats v):
  //   100 0 89 50 10 60 20 70 30 8c 50 8a 50 60 8b 50 60 70 48 5*100 168*1
  //   中間レポート課題　テスト回路
  //   D1 D2   Z1 Z2 Z3 Z4
  //   D1 D2   Z1 Z2 Z3 Z4
  //   エラーの数
  //   エラー発生時赤に点灯
endmodule

module inst_mem (
  input  [31:0] A,
  output [31:0] D
);

  wire [23:0] adder_1_out, adder_2_out, adder_3_out;

  Hex_Digit_Display hex_digit_display_1 (.value(A[31:28]));  // open: dp
  Hex_Digit_Display hex_digit_display_2 (.value(A[27:24]));  // open: dp
  Hex_Digit_Display hex_digit_display_3 (.value(A[23:20]));  // open: dp
  Hex_Digit_Display hex_digit_display_4 (.value(A[15:12]));  // open: dp
  Hex_Digit_Display hex_digit_display_5 (.value(A[19:16]));  // open: dp
  Hex_Digit_Display hex_digit_display_6 (.value(A[7:4]));  // open: dp
  Hex_Digit_Display hex_digit_display_7 (.value(A[11:8]));  // open: dp
  Adder #(.width(24)) adder_1 (.a(A[23:0]), .b(24'h1), .out(adder_1_out));  // open: cin, cout
  Adder #(.width(24)) adder_2 (.a(A[23:0]), .b(24'h2), .out(adder_2_out));  // open: cin, cout
  Adder #(.width(24)) adder_3 (.a(A[23:0]), .b(24'h3), .out(adder_3_out));  // open: cin, cout
  Hex_Digit_Display hex_digit_display_8 (.value(A[3:0]));  // open: dp
  ROM #(.addrWidth(24)) rom_1 (.addr(A[23:0]), .data(D[31:24]));  // open: sel
  ROM #(.addrWidth(24)) rom_2 (.addr(adder_1_out), .data(D[23:16]));  // open: sel
  ROM #(.addrWidth(24)) rom_3 (.addr(adder_2_out), .data(D[15:8]));  // open: sel
  ROM #(.addrWidth(24)) rom_4 (.addr(adder_3_out), .data(D[7:0]));  // open: sel
  Hex_Digit_Display hex_digit_display_9 (.value(D[31:28]));  // open: dp
  Hex_Digit_Display hex_digit_display_10 (.value(D[27:24]));  // open: dp
  Hex_Digit_Display hex_digit_display_11 (.value(D[23:20]));  // open: dp
  Hex_Digit_Display hex_digit_display_12 (.value(D[19:16]));  // open: dp
  Hex_Digit_Display hex_digit_display_13 (.value(D[15:12]));  // open: dp
  Hex_Digit_Display hex_digit_display_14 (.value(D[11:8]));  // open: dp
  Hex_Digit_Display hex_digit_display_15 (.value(D[7:4]));  // open: dp
  Hex_Digit_Display hex_digit_display_16 (.value(D[3:0]));  // open: dp

  // Notes on the sheet:
  //   Address上位8bitは未使用
  //   Address(32b)
  //   contents of rom_1 (hex, n*v repeats v):
  //   3c 1 10 1 34 30 0 0 3c 1 10 1 34 35 0 4c 8e b5 0 0 2 74 90 20 22 10 0 4 22 31 ff ff 16 30 0 5 22 10
  //   ff ff 8e 15 0 0 12 56 0 6 ae 13 0 2 8 0 0 0 22 f0 0 2 2 b7 80 20 2 11 90 25 8 0 0 0 ae 13 0 3 1 8a
  //   88 26 8
  //   contents of rom_2 (hex, n*v repeats v):
  //   3c 1 10 1 34 30 0 0 3c 1 10 1 34 35 0 4c 8e b5 0 0 2 74 90 20 22 10 0 4 22 31 ff ff 16 30 0 5 22 10
  //   ff ff 8e 15 0 0 12 56 0 6 ae 13 0 2 8 0 0 0 22 f0 0 2 2 b7 80 20 2 11 90 25 8 0 0 0 ae 13 0 3 1 8a
  //   88 26 8
  //   contents of rom_3 (hex, n*v repeats v):
  //   3c 1 10 1 34 30 0 0 3c 1 10 1 34 35 0 4c 8e b5 0 0 2 74 90 20 22 10 0 4 22 31 ff ff 16 30 0 5 22 10
  //   ff ff 8e 15 0 0 12 56 0 6 ae 13 0 2 8 0 0 0 22 f0 0 2 2 b7 80 20 2 11 90 25 8 0 0 0 ae 13 0 3 1 8a
  //   88 26 8
  //   contents of rom_4 (hex, n*v repeats v):
  //   3c 1 10 1 34 30 0 0 3c 1 10 1 34 35 0 4c 8e b5 0 0 2 74 90 20 22 10 0 4 22 31 ff ff 16 30 0 5 22 10
  //   ff ff 8e 15 0 0 12 56 0 6 ae 13 0 2 8 0 0 0 22 f0 0 2 2 b7 80 20 2 11 90 25 8 0 0 0 ae 13 0 3 1 8a
  //   88 26 8
  //   Data(32b)
endmodule

module _32b_bus_monitor (
);

  wire [3:0] undriven_2, undriven_3, undriven_4, undriven_5;
  wire [19:0] undriven;

  Hex_Digit_Display hex_digit_display_1 (.value(undriven_5));  // open: dp
  Hex_Digit_Display hex_digit_display_2 (.value(undriven_3));  // open: dp
  Hex_Digit_Display hex_digit_display_3 (.value(undriven_4));  // open: dp
  Hex_Digit_Display hex_digit_display_4 (.value(undriven[15:12]));  // open: dp
  Hex_Digit_Display hex_digit_display_5 (.value(undriven[19:16]));  // open: dp
  Hex_Digit_Display hex_digit_display_6 (.value(undriven_2));  // open: dp
  Hex_Digit_Display hex_digit_display_7 (.value(undriven[3:0]));  // open: dp
  Hex_Digit_Display hex_digit_display_8 (.value(undriven[7:4]));  // open: dp

  // Notes on the sheet:
  //   上位ビット側
  //   下位ビット側
  //   32bitバスの論理値を4bit毎の16進数でモニターする
  //   コピーペーストを使って他の回路で使用すること
endmodule

module alu8 (
  input  [7:0] A,
  input  [7:0] B,
  input  [3:0] S,
  output [7:0] X,
  output NZ,
  output Cout,
  output OV
);

  wire alu1_1_cout, alu1_2_cout, alu1_3_cout, alu1_4_cout, alu1_5_cout, alu1_6_cout, alu1_7_cout,
       alu1_8_b_prime, and_1_out, and_2_out, comparator_1_eq, not_1_out, not_2_out, not_3_out, or_1_out,
       sel_dec_1_cin, sel_dec_1_s30, sel_dec_1_s40, sel_dec_1_s50;
  wire [2:0] sel_dec_1_s10;
  wire [7:0] multiplexer_1_out, multiplexer_2_out;

  sel_dec sel_dec_1 (
    .S0(S[0]), .S1(S[1]), .S2(S[2]), .S3(S[3]), .S10(sel_dec_1_s10[0]), .S30(sel_dec_1_s30),
    .S20(sel_dec_1_s10[1]), .S21(sel_dec_1_s10[2]), .S40(sel_dec_1_s40), .Cin(sel_dec_1_cin),
    .S50(sel_dec_1_s50));
  Multiplexer #(.width(8), .enable("false")) multiplexer_1 (
    .in0({8{1'b0}}), .in1(A), .out(multiplexer_1_out), .sel(sel_dec_1_s40));
  Multiplexer #(.width(8), .enable("false")) multiplexer_2 (
    .in0(B), .in1(8'h1), .out(multiplexer_2_out), .sel(sel_dec_1_s30));
  alu1 alu1_1 (
    .A(multiplexer_1_out[0]), .B(multiplexer_2_out[0]), .Cin(sel_dec_1_cin), .S21(sel_dec_1_s10[2]),
    .S10(sel_dec_1_s10[0]), .X(X[0]), .Cout(alu1_1_cout), .S20(sel_dec_1_s10[1]));  // open: B_prime
  alu1 alu1_2 (
    .A(multiplexer_1_out[1]), .B(multiplexer_2_out[1]), .Cin(alu1_1_cout), .S21(sel_dec_1_s10[2]),
    .S10(sel_dec_1_s10[0]), .X(X[1]), .Cout(alu1_2_cout), .S20(sel_dec_1_s10[1]));  // open: B_prime
  alu1 alu1_3 (
    .A(multiplexer_1_out[2]), .B(multiplexer_2_out[2]), .Cin(alu1_2_cout), .S21(sel_dec_1_s10[2]),
    .S10(sel_dec_1_s10[0]), .X(X[2]), .Cout(alu1_3_cout), .S20(sel_dec_1_s10[1]));  // open: B_prime
  alu1 alu1_4 (
    .A(multiplexer_1_out[3]), .B(multiplexer_2_out[3]), .Cin(alu1_3_cout), .S21(sel_dec_1_s10[2]),
    .S10(sel_dec_1_s10[0]), .X(X[3]), .Cout(alu1_4_cout), .S20(sel_dec_1_s10[1]));  // open: B_prime
  alu1 alu1_5 (
    .A(multiplexer_1_out[4]), .B(multiplexer_2_out[4]), .Cin(alu1_4_cout), .S21(sel_dec_1_s10[2]),
    .S10(sel_dec_1_s10[0]), .X(X[4]), .Cout(alu1_5_cout), .S20(sel_dec_1_s10[1]));  // open: B_prime
  alu1 alu1_6 (
    .A(multiplexer_1_out[5]), .B(multiplexer_2_out[5]), .Cin(alu1_5_cout), .S21(sel_dec_1_s10[2]),
    .S10(sel_dec_1_s10[0]), .X(X[5]), .Cout(alu1_6_cout), .S20(sel_dec_1_s10[1]));  // open: B_prime
  alu1 alu1_7 (
    .A(multiplexer_1_out[6]), .B(multiplexer_2_out[6]), .Cin(alu1_6_cout), .S21(sel_dec_1_s10[2]),
    .S10(sel_dec_1_s10[0]), .X(X[6]), .Cout(alu1_7_cout), .S20(sel_dec_1_s10[1]));  // open: B_prime
  alu1 alu1_8 (
    .A(multiplexer_1_out[7]), .B(multiplexer_2_out[7]), .Cin(alu1_7_cout), .S21(sel_dec_1_s10[2]),
    .S10(sel_dec_1_s10[0]), .X(X[7]), .Cout(Cout), .S20(sel_dec_1_s10[1]), .B_prime(alu1_8_b_prime));
  not not_1 (not_1_out, multiplexer_1_out[7]);
  not not_2 (not_2_out, alu1_8_b_prime);
  not not_3 (not_3_out, X[7]);
  and and_1 (and_1_out, not_1_out, not_2_out, X[7]);
  and and_2 (and_2_out, multiplexer_1_out[7], alu1_8_b_prime, not_3_out);
  Comparator comparator_1 (.a(X), .b({8{1'b0}}), .eq(comparator_1_eq));  // open: gt, lt
  or or_1 (or_1_out, and_1_out, and_2_out);
  not not_4 (NZ, comparator_1_eq);
  Multiplexer #(.enable("false")) multiplexer_3 (.in0(or_1_out), .in1(1'b0), .out(OV), .sel(sel_dec_1_s50));

  // Notes on the sheet:
  //   M3
  //   M4
  //   M5
endmodule

module test_alu_random_arith (
);

  wire alu8_1_cout, alu8_1_nz, alu8_1_ov, and_1_out, CK_out, comparator_1_eq, comparator_2_eq,
       comparator_3_eq, comparator_4_eq, comparator_5_eq, d_ff_1_q, not_1_out, or_1_out;
  wire [7:0] alu8_1_x, counter_2_q;
  wire [9:0] adder_1_out, counter_1_q;
  wire [31:0] rom_1_data;

  Clock CK (.out(CK_out));
  Counter #(.width(10), .max('h3ff)) counter_1 (
    .D(adder_1_out), .Q(counter_1_q), .clk(CK_out), .clr(comparator_1_eq));  // open: load, count, carry
  Adder #(.width(10)) adder_1 (.a(10'h1), .b(counter_1_q), .out(adder_1_out));  // open: cin, cout
  Comparator #(.width(10)) comparator_1 (.a(adder_1_out), .b({10{1'b1}}), .eq(comparator_1_eq));  // open: gt, lt
  ROM #(.addrWidth(10), .dataWidth(32)) rom_1 (.addr(counter_1_q), .data(rom_1_data));  // open: sel
  Hex_Digit_Display hex_digit_display_1 (.value(rom_1_data[7:4]));  // open: dp
  Hex_Digit_Display hex_digit_display_2 (.value(rom_1_data[31:28]));  // open: dp
  Hex_Digit_Display hex_digit_display_3 (.value(rom_1_data[27:24]));  // open: dp
  Hex_Digit_Display hex_digit_display_4 (.value(rom_1_data[23:20]));  // open: dp
  Hex_Digit_Display hex_digit_display_5 (.value(rom_1_data[19:16]));  // open: dp
  Hex_Digit_Display hex_digit_display_6 (.value(alu8_1_x[7:4]));  // open: dp
  alu8 alu8_1 (
    .A(rom_1_data[31:24]), .B(rom_1_data[23:16]), .X(alu8_1_x), .Cout(alu8_1_cout), .NZ(alu8_1_nz),
    .S(rom_1_data[7:4]), .OV(alu8_1_ov));
  Hex_Digit_Display hex_digit_display_7 (.value(alu8_1_x[3:0]));  // open: dp
  Comparator comparator_2 (.a(rom_1_data[15:8]), .b(alu8_1_x), .eq(comparator_2_eq));  // open: gt, lt
  Comparator #(.width(1)) comparator_3 (.a(alu8_1_cout), .b(rom_1_data[2]), .eq(comparator_3_eq));  // open: gt, lt
  Comparator #(.width(1)) comparator_4 (.a(alu8_1_nz), .b(rom_1_data[0]), .eq(comparator_4_eq));  // open: gt, lt
  Comparator #(.width(1)) comparator_5 (.a(alu8_1_ov), .b(rom_1_data[1]), .eq(comparator_5_eq));  // open: gt, lt
  or or_1 (or_1_out, comparator_3_eq, rom_1_data[7]);
  not not_1 (not_1_out, and_1_out);
  and and_1 (and_1_out, comparator_2_eq, or_1_out, comparator_4_eq, comparator_5_eq);
  LED led_1 (.in(and_1_out));
  Counter counter_2 (
    .D({8{1'b0}}), .count(not_1_out), .Q(counter_2_q), .clk(CK_out), .clr(comparator_1_eq));  // open: load, carry
  Hex_Digit_Display hex_digit_display_8 (.value(counter_2_q[7:4]));  // open: dp
  D_Flip_Flop d_ff_1 (.clk(CK_out), .D(not_1_out), .Q(d_ff_1_q), .en(not_1_out));  // open: Qn, preset, reset
  Hex_Digit_Display hex_digit_display_9 (.value(counter_2_q[3:0]));  // open: dp
  LED led_2 (.in(d_ff_1_q));

  // Notes on the sheet:
  //   contents of rom_1 (hex, n*v repeats v):
  //   e1875a15 dc01db35 a001a121 ae01ad35 8b1aa501 75472e15 61016035 78542415 f501f621 62e84a05 808ef211
  //   9c019d21 b010c21 41014221 d901da21 9559ee01 45e6201 fc01fd21 e301e421 ec5a4605 ca01c935 580e4a15
  //   3a235d01 72017135 aa6c1605 e0e1c105 65a60b05 bd01bc35 3b013a35 f4a99d05 eb01ec21 e03a1a05 9442d601
  //   2c0e1e15 96019535 6d7ce903 a87c2c17 f201f135 5010621 b001af35 3010421 5e015d35 77017821 23012235
  //   ac01ad21 5450a403 d725fc01 38013921 51ea6711 dc01dd21 2a65c11 48014735 b801b735 c101c221 5f90cf13
  //   d601d535 65016435 6cd54105 a201a321 8010735 90841407 1a1a201 d6e6f011 6658be03 40013f35 bb01ba35
  //   b4651905 d5c39805 cc0bd701 843b4917 23012421 ce01cd35 73a91c05 d8b62215 df11c11 e224be15 58015735
  //   dbfdde11 64ca9a13 71017035 a59f0615 b700b715 74c6ae13 a91cc501 f701f821 3ac70105 6b016a35 bd01be21
  //   f011021 b1e09105 25012435 66016535 bce9d311 fe090705 3c013b35 9fa4fb11 15a5b01 1ff31 50a6f601
  //   9c28c401 8e018d35 23012235 93019421 be72411 5c8feb01 45014435 97019821 8e018d35 aa0ab401 cca87407
  //   59015835 762da303 18364e01 4010335 91019035 c501c435 2158c911 be01bf21 348dc101 5e015f21 bf328d15
  //   25012621 4ac78313 8fe77607 573d1a15 e301e421 f79e9505 c001bf35 ed01ec35 73017421 c3a26507 7b860105
  //   86018721 c901ca21 2b8eb901 9f019e35 d801d735 1f011e35 6d016c35 e000e015 37013635 2167ba11 90a4ec11
  //   82602217 c301c421 3c013d21 b1bc6d07 550d4815 ce01cd35 42014135 94019335 f32a1d05 8b4f3c17 43014235
  //   68323615 38013921 fcbab605 a7903707 dd01dc35 320e311 1d011e21 8f058a15 65016621 2ab37711 4c014d21
  //   6b135815 c7facd11 c301c235 fb01fa35 de489615 e901e835 903b5517 990fa801 d201d321 dd01de21 ca01cb21
  //   bd01be21 d701d635 2b83a813 1233df11 94722217 c101c035 60015f35 b38f4207 8d0c8115 81740d17 d8ecc405
  //   1dd34a11 41014221 42014321 c801c921 9e019d15 a801a735 c701c635 8e018d35 62016135 78017921 3fafd01
  //   3b013c21 ad01ac35 e101e221 faaea805 600b5515 56015721 67016635 d7885f07 1960b911 87018635 1e78a611
  //   4cde2a05 58015735 b3eda005 da26b11 31013221 7368db03 d609df01 db21fc01 57c81f05 ef01f021 f3fbf811
  //   bf06b915 aefab411 8ee37107 cb01ca35 a601a721 97019635 96019721 da01db21 a4228215 8a58e201 62016321
  //   97019635 9f01a021 ead6c005 2e8ab801 eb01ec21 39013815 26173d01 1edffd01 f101f035 ff010024 140d0715
  //   91019035 ef01ee35 d0319f15 8ba4e711 a401a335 95019621 9045d501 3e013d35 8262e01 7365d803 c46c611
  //   e001e101 7a4ab01 c0c28205 2e2a5801 7489eb13 d401d521 49014835 65570e15 f5463b05 124ec411 b7b56c07
  //   4fa0af13 26012535 a801a735 5010435 a97e2705 ba1c9e15 c301c235 3f013e35 7693e313 a71e8915 2ba38813
  //   80018121 75017435 c601c721 ca5f2905 25a38213 c101c035 af01b021 78981005 55015621 c28f5107 d30add01
  //   d000d15 b701b821 5b76d103 d9421b05 a101a221 68016921 54429603 3ddb1805 2555d011 468abc13 8967211
  //   27012821 262a5001 5d82df01 4b9fac13 89018835 e0765605 ac01ad21 9f019e35 7ba72205 81018221 1c021a15
  //   9654ea01 db01dc21 be605e17 c201c321 88a0e811 1f011e35 9b376417 52015321 77017821 7c017d21 76017721
  //   e6767017 43014421 3c013b35 552d8203 f101f035 b192401 5c015b35 70ef5f05 7da92605 e301e421 64cb2f05
  //   23d3f01 ac01ab35 bb01ba35 8ce67207 4b014a35 6cd49813 8d018e21 b40cb11 e901e835 7c7af603 c801c735
  //   c101c221 58015921 a1b8e911 fc01fb35 8969e01 c601c721 21012221 c701c635 d601d535 1b011c21 87018821
  //   fe01ff21 161afc11 4869df11 99019835 1f012021 485aa203 cf01ce35 93019235 f6ce2815 56ec4205 93019421
  //   a901aa21 8f018e35 badbdf11 e0509015 bbfdbe11 5a015935 cd01cc35 bd01be21 59c09913 a501a621 70b1bf13
  //   6fc6a913 fbcdc805 35da5b11 e101e221 51015221 7982f713 45c18413 d71cbb15 d401d335 d1deaf05 a501a435
  //   df01de35 d201d321 18011921 2a6f9903 fa01fb21 16b9cf01 c001c121 5b81da13 75c8ad13 2f013021 bdbe601
  //   5e026001 b010a35 73017235 cf01ce35 20012121 3a013b21 52015321 6a016935 c3586b17 e201e135 de01df21
  //   8081001 4c173515 23b37011 97019635 14def201 8d018c35 771a5d15 79f18813 fcd1cd05 4e014f21 d010c35
  //   4a014935 28979113 c35e6517 68016921 20da4611 3b380315 2a012b21 39013835 31013221 8c018b35 c301c235
  //   785dd503 df01e021 df785705 f401f335 c901ca21 3010421 67016635 bcc78305 dbb5211 78017921 1010221
  //   58b5a313 45e22705 ec01ed21 a901a835 34013521 af924107 e201e321 3f013e35 140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
  //   0: 加算
  //   1: 減算
  //   2: 1加算
  //   3: 1減算
  //   S入力
  //   A入力
  //   8: Bの否定
  //   9: 論理積
  //   14: 論理和
  //   15: 排他的論理和
  //   B入力
  //   X出力
  //   エラーの数
  //   エラー発生時赤に点灯
endmodule

module test_alu_random_logic (
);

  wire alu8_1_cout, alu8_1_nz, alu8_1_ov, and_1_out, CK_out, comparator_1_eq, comparator_2_eq,
       comparator_3_eq, comparator_4_eq, comparator_5_eq, d_ff_1_q, not_1_out, or_1_out;
  wire [7:0] alu8_1_x, counter_2_q;
  wire [9:0] adder_1_out, counter_1_q;
  wire [31:0] rom_1_data;

  Clock CK (.out(CK_out));
  Counter #(.width(10), .max('h3ff)) counter_1 (
    .D(adder_1_out), .Q(counter_1_q), .clk(CK_out), .clr(comparator_1_eq));  // open: load, count, carry
  Adder #(.width(10)) adder_1 (.a(10'h1), .b(counter_1_q), .out(adder_1_out));  // open: cin, cout
  Comparator #(.width(10)) comparator_1 (.a(adder_1_out), .b({10{1'b1}}), .eq(comparator_1_eq));  // open: gt, lt
  ROM #(.addrWidth(10), .dataWidth(32)) rom_1 (.addr(counter_1_q), .data(rom_1_data));  // open: sel
  Hex_Digit_Display hex_digit_display_1 (.value(rom_1_data[7:4]));  // open: dp
  Hex_Digit_Display hex_digit_display_2 (.value(rom_1_data[27:24]));  // open: dp
  Hex_Digit_Display hex_digit_display_3 (.value(rom_1_data[31:28]));  // open: dp
  Hex_Digit_Display hex_digit_display_4 (.value(rom_1_data[19:16]));  // open: dp
  Hex_Digit_Display hex_digit_display_5 (.value(rom_1_data[23:20]));  // open: dp
  Hex_Digit_Display hex_digit_display_6 (.value(alu8_1_x[7:4]));  // open: dp
  alu8 alu8_1 (
    .A(rom_1_data[31:24]), .B(rom_1_data[23:16]), .X(alu8_1_x), .Cout(alu8_1_cout), .NZ(alu8_1_nz),
    .S(rom_1_data[7:4]), .OV(alu8_1_ov));
  Hex_Digit_Display hex_digit_display_7 (.value(alu8_1_x[3:0]));  // open: dp
  Comparator comparator_2 (.a(rom_1_data[15:8]), .b(alu8_1_x), .eq(comparator_2_eq));  // open: gt, lt
  Comparator #(.width(1)) comparator_3 (.a(alu8_1_cout), .b(rom_1_data[2]), .eq(comparator_3_eq));  // open: gt, lt
  Comparator #(.width(1)) comparator_4 (.a(alu8_1_nz), .b(rom_1_data[0]), .eq(comparator_4_eq));  // open: gt, lt
  Comparator #(.width(1)) comparator_5 (.a(alu8_1_ov), .b(rom_1_data[1]), .eq(comparator_5_eq));  // open: gt, lt
  or or_1 (or_1_out, comparator_3_eq, rom_1_data[7]);
  not not_1 (not_1_out, and_1_out);
  and and_1 (and_1_out, comparator_2_eq, or_1_out, comparator_4_eq, comparator_5_eq);
  LED led_1 (.in(and_1_out));
  Counter counter_2 (
    .D({8{1'b0}}), .count(not_1_out), .Q(counter_2_q), .clk(CK_out), .clr(comparator_1_eq));  // open: load, carry
  Hex_Digit_Display hex_digit_display_8 (.value(counter_2_q[7:4]));  // open: dp
  D_Flip_Flop d_ff_1 (.clk(CK_out), .D(not_1_out), .Q(d_ff_1_q), .en(not_1_out));  // open: Qn, preset, reset
  Hex_Digit_Display hex_digit_display_9 (.value(counter_2_q[3:0]));  // open: dp
  LED led_2 (.in(d_ff_1_q));

  // Notes on the sheet:
  //   contents of rom_1 (hex, n*v repeats v):
  //   d9ac5381 fd707091 ff434391 36430291 ea4aeae1 7e2856f1 8ee1181 555702f1 de5e8f1 929597e1 c762e7e1
  //   362cd381 1f5f4f1 e8120090 6c424091 e38d6ef1 c91be481 762e2691 bf68ffe1 741d7de1 22d50090 18cddde1
  //   a847eff1 4caf5081 27807f81 62976881 820090 8fc08091 428e7181 c8a9e9e1 9ecc3381 e251b3f1 550757e1
  //   f17a8bf1 9d010191 65ef6591 2944bb81 570d5fe1 ea867981 f5fcf491 16eb0291 2358a781 16dd2281 9f3e1e91
  //   f425f5e1 46f5b3f1 588bd3f1 5eacf2f1 4027d881 dc07dbf1 e42dc9f1 217352f1 92df9291 bd6d2d91 6bd84891
  //   f84db5f1 3efd3c91 622d2091 f2b240f1 9c059de1 4824db81 21b19f1 d8cdc891 214565e1 8e70fee1 e4c8c091
  //   204ab581 fda459f1 2f2c2c91 6b24d81 6af5081 3cec2c91 41cd4191 f1a8a091 c18041f1 fdafffe1 b331b3e1
  //   d97ca5f1 9523b7e1 300bf481 801c9ce1 fbf00bf1 1cf91891 92bc4381 14f2f6e1 32db1291 d6b8fee1 e8638bf1
  //   2b20291 dc9b9891 ed06ebf1 79156cf1 e732d5f1 ecbe52f1 4c5b4891 d2270291 99a15e81 4ef2bcf1 e3180090
  //   b5383091 9438bce1 822dd281 34e2d6f1 617e7fe1 a542e7e1 7218e781 214465e1 9545de1 d74f4791 98c25af1
  //   f9857a81 8e040491 9db59591 4d820090 c0c53a81 7ed1ffe1 404606f1 722b59f1 bd5dfde1 514819f1 8c570491
  //   457575e1 49788781 e2c725f1 b6f00f81 7cab2891 d6eefee1 2b4db281 904eb181 a7916e81 3d607de1 45840491
  //   eea3efe1 c498dce1 4b996681 9f0b0b91 5905fa81 2144bb81 8f22afe1 7b087be1 f7ba4581 79dc2381 5d267fe1
  //   b2ee5cf1 b2a7b7e1 49531af1 26890090 a08b8091 b0131091 73768981 fb42fbe1 6f534391 f2a45b81 1757a881
  //   5d000090 8df30c81 4c946b81 adf90681 4afd0281 661076e1 89320090 653bc481 861c9af1 655f7fe1 d7a18191
  //   c30a0291 25496de1 2aebebe1 78cbb3f1 74c2f6e1 601272e1 ca2aee1 aba6a291 76e46491 998199e1 d220f2f1
  //   d7ab8391 68fd6891 a73bc481 adbfbfe1 f892fae1 2ed5ffe1 66deb8f1 77dea9f1 4e515fe1 cad71df1 83966981
  //   31703091 44574491 75c0b5f1 83010191 bbc8fbe1 9e05fa81 38b0391 15440491 cda3efe1 e66c9381 779b6481
  //   996dfde1 3d767fe1 184db281 e529ccf1 ef0b0b91 73f9fbe1 8c4dc1f1 88f1f9e1 850c8de1 27f30c81 22782091
  //   221735f1 9bd62981 5d474591 b4f90681 9c5fdfe1 d8a870f1 a33fc081 b817bfe1 d58ddde1 113131e1 89179fe1
  //   34713091 cd18d5f1 57705091 5fcd4d91 e77c6491 f716e1f1 42cfcfe1 352637e1 b43d3491 da63b9f1 7d7b7fe1
  //   f040491 51444091 e914eb81 930697e1 68e61981 30e9f9e1 a41be481 f83fffe1 eac02af1 aec967f1 ef3ac581
  //   584fb081 6afc96f1 7982fbe1 b22c2091 26180090 29cfefe1 46aceee1 b111a0f1 60caeae1 49c14191 b41bbfe1
  //   ac1a0891 a0c68091 8e76f8f1 7a537be1 ba76ccf1 67b6f7e1 55c297f1 d84bdbe1 e17b6191 adec41f1 d8ec1381
  //   3b665df1 fa18e781 a4fb5ff1 a341e2f1 31af2191 c47a4091 cb948091 51dcdde1 90531091 45fd0281 3aa22291
  //   8cb44b81 e2629d81 68557de1 2ba78cf1 43e61981 12ca3581 d5fc0381 c85890f1 2c430090 5c8cdce1 bded5f1
  //   347676e1 7c1c7ce1 713f3191 c342c3e1 dbf0d091 e54cede1 eacfca91 87fbffe1 fd37caf1 d1888091 ef6c6c91
  //   90d0d0e1 78e16091 dce23ef1 27d8ffe1 df27f8f1 d6808091 96a2b6e1 e2cfc291 9ff80781 97c38391 7847b881
  //   84d58491 baf10e81 becc8c91 27db2481 34272491 bae55ff1 a1d48091 e9779ef1 c5fbffe1 e17a6091 ecfdec91
  //   641773f1 e4fae091 8b12ed81 f676f6e1 9ea08091 83fe7df1 c2fa0581 48d59df1 2f2dd281 840ff081 21d1f1e1
  //   6ab02091 cba1ebe1 a99c35f1 ee39ffe1 f17c7091 f06898f1 bbf6ffe1 73c4f7e1 c5ab5481 ea907af1 f911f9e1
  //   9d189de1 b7000090 f08f781 c37c8381 d764f7e1 41350191 38360ef1 86a18091 27082ff1 a0cfefe1 7dbfffe1
  //   ea3afae1 89808091 f3fc081 3593a6f1 39132af1 8b908091 643d2491 2e363ee1 1206f981 28b4bce1 d161f1e1
  //   28547cf1 4f320291 e9c9c991 f303fc81 97889fe1 337d4ef1 39f83891 1f534cf1 9863fbf1 d84ddde1 9e30191
  //   edbb56f1 32c3f1f1 d783d7e1 a512b7f1 4738c81 d156d7e1 37b73791 d4a05f81 276641f1 6b0090 9bb922f1
  //   35202091 8045ba81 66fd9bf1 a745e7e1 d8d5d091 2ae8c2f1 3fafbe1 b209bbf1 1b12ed81 5ece9f1 abd7ffe1
  //   b2d5f7e1 c7ee1181 b6898091 c257d7e1 622062e1 6a2c46f1 fbb34c81 399ba2f1 b9c3fbe1 f768ffe1 39743091
  //   c865adf1 88f0f8e1 9c877881 3f89bfe1 6cb1ddf1 707303f1 e157f7e1 5a3ac581 237577e1 f2d0d91 98e0891
  //   9f7d8281 e7b7a791 61cdacf1 a4e1e5e1 724d7fe1 e7d037f1 7ad0aaf1 73830391 5d48b781 cff0c91 68ba2891
  //   82c03f81 10887781 ab302091 61950191 7ef80781 b3c3f3e1 870df281 34aa5581 5ec29cf1 72a4f6e1 9464ff1
  //   ee7d8281 3258a781 4a6a4a91 c21c0090 cb0ff081 45490cf1 11c2d3f1 203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
  //   0: 加算
  //   1: 減算
  //   2: 1加算
  //   3: 1減算
  //   S入力
  //   A入力
  //   8: Bの否定
  //   9: 論理積
  //   14: 論理和
  //   15: 排他的論理和
  //   B入力
  //   X出力
  //   エラーの数
  //   エラー発生時赤に点灯
endmodule

module test_alu_add (
);

  wire alu8_1_cout, alu8_1_nz, alu8_1_ov, and_1_out, CK_out, comparator_1_eq, comparator_2_eq,
       comparator_3_eq, comparator_4_eq, comparator_5_eq, d_ff_1_q, not_1_out, or_1_out;
  wire [7:0] alu8_1_x, counter_2_q;
  wire [9:0] adder_1_out, counter_1_q;
  wire [31:0] rom_1_data;

  Clock CK (.out(CK_out));
  Counter #(.width(10), .max('h3ff)) counter_1 (
    .D(adder_1_out), .Q(counter_1_q), .clk(CK_out), .clr(comparator_1_eq));  // open: load, count, carry
  Adder #(.width(10)) adder_1 (.a(10'h1), .b(counter_1_q), .out(adder_1_out));  // open: cin, cout
  Comparator #(.width(10)) comparator_1 (.a(adder_1_out), .b(10'h42), .eq(comparator_1_eq));  // open: gt, lt
  ROM #(.addrWidth(10), .dataWidth(32)) rom_1 (.addr(counter_1_q), .data(rom_1_data));  // open: sel
  Hex_Digit_Display hex_digit_display_1 (.value(rom_1_data[7:4]));  // open: dp
  Hex_Digit_Display hex_digit_display_2 (.value(rom_1_data[27:24]));  // open: dp
  Hex_Digit_Display hex_digit_display_3 (.value(rom_1_data[31:28]));  // open: dp
  Hex_Digit_Display hex_digit_display_4 (.value(rom_1_data[19:16]));  // open: dp
  Hex_Digit_Display hex_digit_display_5 (.value(rom_1_data[23:20]));  // open: dp
  Hex_Digit_Display hex_digit_display_6 (.value(alu8_1_x[7:4]));  // open: dp
  alu8 alu8_1 (
    .A(rom_1_data[31:24]), .B(rom_1_data[23:16]), .X(alu8_1_x), .Cout(alu8_1_cout), .NZ(alu8_1_nz),
    .S(rom_1_data[7:4]), .OV(alu8_1_ov));
  Hex_Digit_Display hex_digit_display_7 (.value(alu8_1_x[3:0]));  // open: dp
  Comparator comparator_2 (.a(rom_1_data[15:8]), .b(alu8_1_x), .eq(comparator_2_eq));  // open: gt, lt
  Comparator #(.width(1)) comparator_3 (.a(alu8_1_cout), .b(rom_1_data[2]), .eq(comparator_3_eq));  // open: gt, lt
  Comparator #(.width(1)) comparator_4 (.a(alu8_1_nz), .b(rom_1_data[0]), .eq(comparator_4_eq));  // open: gt, lt
  Comparator #(.width(1)) comparator_5 (.a(alu8_1_ov), .b(rom_1_data[1]), .eq(comparator_5_eq));  // open: gt, lt
  or or_1 (or_1_out, comparator_3_eq, rom_1_data[7]);
  not not_1 (not_1_out, and_1_out);
  LED led_1 (.in(and_1_out));
  and and_1 (and_1_out, comparator_2_eq, or_1_out, comparator_4_eq, comparator_5_eq);
  Counter counter_2 (
    .D({8{1'b0}}), .count(not_1_out), .Q(counter_2_q), .clk(CK_out), .clr(comparator_1_eq));  // open: load, carry
  Hex_Digit_Display hex_digit_display_8 (.value(counter_2_q[7:4]));  // open: dp
  D_Flip_Flop d_ff_1 (.clk(CK_out), .D(not_1_out), .Q(d_ff_1_q), .en(not_1_out));  // open: Qn, preset, reset
  Hex_Digit_Display hex_digit_display_9 (.value(counter_2_q[3:0]));  // open: dp
  LED led_2 (.in(d_ff_1_q));

  // Notes on the sheet:
  //   contents of rom_1 (hex, n*v repeats v):
  //   10101 20201 40401 80801 101001 202001 404001 808001 1010201 1030401 1070801 10f1001 11f2001 13f4001
  //   17f8003 1ff0004 ff010004 ff030205 ff070605 ff0f0e05 ff1f1e05 ff3f3e05 ff7f7e05 fffffe05 1000101
  //   2000201 4000401 8000801 10001001 20002001 40004001 80008001 1010201 3010401 7010801 f011001 1f012001
  //   3f014001 7f018003 ff010004 1ff0004 3ff0205 7ff0605 fff0e05 1fff1e05 3fff3e05 7fff7e05 fffffe05
  //   1ff0004 3fd0004 7f90004 ff10004 1fe10004 3fc10004 7f810004 ff010004 ff010004 fd030004 f9070004
  //   f10f0004 e11f0004 c13f0004 817f0004 1ff0004
  //   0: 加算
  //   1: 減算
  //   2: 1加算
  //   3: 1減算
  //   S入力
  //   A入力
  //   8: Bの否定
  //   9: 論理積
  //   14: 論理和
  //   15: 排他的論理和
  //   B入力
  //   X出力
  //   エラーの数
  //   エラー発生時赤に点灯
endmodule

module test_alu_sub (
);

  wire alu8_1_cout, alu8_1_nz, alu8_1_ov, and_1_out, CK_out, comparator_1_eq, comparator_2_eq,
       comparator_3_eq, comparator_4_eq, comparator_5_eq, d_ff_1_q, not_1_out, or_1_out;
  wire [7:0] alu8_1_x, counter_2_q;
  wire [9:0] adder_1_out, counter_1_q;
  wire [31:0] rom_1_data;

  Clock CK (.out(CK_out));
  Counter #(.width(10), .max('h3ff)) counter_1 (
    .D(adder_1_out), .Q(counter_1_q), .clk(CK_out), .clr(comparator_1_eq));  // open: load, count, carry
  Adder #(.width(10)) adder_1 (.a(10'h1), .b(counter_1_q), .out(adder_1_out));  // open: cin, cout
  Comparator #(.width(10)) comparator_1 (.a(adder_1_out), .b(10'h42), .eq(comparator_1_eq));  // open: gt, lt
  ROM #(.addrWidth(10), .dataWidth(32)) rom_1 (.addr(counter_1_q), .data(rom_1_data));  // open: sel
  Hex_Digit_Display hex_digit_display_1 (.value(rom_1_data[7:4]));  // open: dp
  Hex_Digit_Display hex_digit_display_2 (.value(rom_1_data[31:28]));  // open: dp
  Hex_Digit_Display hex_digit_display_3 (.value(rom_1_data[27:24]));  // open: dp
  Hex_Digit_Display hex_digit_display_4 (.value(rom_1_data[19:16]));  // open: dp
  Hex_Digit_Display hex_digit_display_5 (.value(rom_1_data[23:20]));  // open: dp
  Hex_Digit_Display hex_digit_display_6 (.value(alu8_1_x[7:4]));  // open: dp
  alu8 alu8_1 (
    .A(rom_1_data[31:24]), .B(rom_1_data[23:16]), .X(alu8_1_x), .Cout(alu8_1_cout), .NZ(alu8_1_nz),
    .S(rom_1_data[7:4]), .OV(alu8_1_ov));
  Hex_Digit_Display hex_digit_display_7 (.value(alu8_1_x[3:0]));  // open: dp
  Comparator comparator_2 (.a(rom_1_data[15:8]), .b(alu8_1_x), .eq(comparator_2_eq));  // open: gt, lt
  Comparator #(.width(1)) comparator_3 (.a(alu8_1_cout), .b(rom_1_data[2]), .eq(comparator_3_eq));  // open: gt, lt
  Comparator #(.width(1)) comparator_4 (.a(alu8_1_nz), .b(rom_1_data[0]), .eq(comparator_4_eq));  // open: gt, lt
  Comparator #(.width(1)) comparator_5 (.a(alu8_1_ov), .b(rom_1_data[1]), .eq(comparator_5_eq));  // open: gt, lt
  or or_1 (or_1_out, comparator_3_eq, rom_1_data[7]);
  not not_1 (not_1_out, and_1_out);
  LED led_1 (.in(and_1_out));
  and and_1 (and_1_out, comparator_2_eq, or_1_out, comparator_4_eq, comparator_5_eq);
  Counter counter_2 (
    .D({8{1'b0}}), .count(not_1_out), .Q(counter_2_q), .clk(CK_out), .clr(comparator_1_eq));  // open: load, carry
  Hex_Digit_Display hex_digit_display_8 (.value(counter_2_q[7:4]));  // open: dp
  D_Flip_Flop d_ff_1 (.clk(CK_out), .D(not_1_out), .Q(d_ff_1_q), .en(not_1_out));  // open: Qn, preset, reset
  Hex_Digit_Display hex_digit_display_9 (.value(counter_2_q[3:0]));  // open: dp
  LED led_2 (.in(d_ff_1_q));

  // Notes on the sheet:
  //   contents of rom_1 (hex, n*v repeats v):
  //   1ff11 2fe11 4fc11 8f811 10f011 20e011 40c011 808013 1010014 103fe11 107fa11 10ff211 11fe211 13fc211
  //   17f8211 1ff0211 ff01fe15 ff03fc15 ff07f815 ff0ff015 ff1fe015 ff3fc015 ff7f8015 ffff0014 1000115
  //   2000215 4000415 8000815 10001015 20002015 40004015 80008015 1010014 3010215 7010615 f010e15 1f011e15
  //   3f013e15 7f017e15 ff01fe15 1ff0211 3ff0411 7ff0811 fff1011 1fff2011 3fff4011 7fff8013 ffff0014
  //   1010014 3030014 7070014 f0f0014 1f1f0014 3f3f0014 7f7f0014 ffff0014
  //   0: 加算
  //   1: 減算
  //   2: 1加算
  //   3: 1減算
  //   S入力
  //   A入力
  //   8: Bの否定
  //   9: 論理積
  //   14: 論理和
  //   15: 排他的論理和
  //   B入力
  //   X出力
  //   エラーの数
  //   エラー発生時赤に点灯
endmodule

module test_alu_inc (
);

  wire alu8_1_cout, alu8_1_nz, alu8_1_ov, and_1_out, CK_out, comparator_1_eq, comparator_2_eq,
       comparator_3_eq, comparator_4_eq, comparator_5_eq, d_ff_1_q, not_1_out, or_1_out;
  wire [7:0] alu8_1_x, counter_2_q;
  wire [9:0] adder_1_out, counter_1_q;
  wire [31:0] rom_1_data;

  Clock CK (.out(CK_out));
  Counter #(.width(10), .max('h3ff)) counter_1 (
    .D(adder_1_out), .Q(counter_1_q), .clk(CK_out), .clr(comparator_1_eq));  // open: load, count, carry
  Adder #(.width(10)) adder_1 (.a(10'h1), .b(counter_1_q), .out(adder_1_out));  // open: cin, cout
  Comparator #(.width(10)) comparator_1 (.a(adder_1_out), .b(10'h12), .eq(comparator_1_eq));  // open: gt, lt
  ROM #(.addrWidth(10), .dataWidth(32)) rom_1 (.addr(counter_1_q), .data(rom_1_data));  // open: sel
  Hex_Digit_Display hex_digit_display_1 (.value(rom_1_data[7:4]));  // open: dp
  Hex_Digit_Display hex_digit_display_2 (.value(rom_1_data[31:28]));  // open: dp
  Hex_Digit_Display hex_digit_display_3 (.value(rom_1_data[27:24]));  // open: dp
  Hex_Digit_Display hex_digit_display_4 (.value(rom_1_data[23:20]));  // open: dp
  Hex_Digit_Display hex_digit_display_5 (.value(rom_1_data[19:16]));  // open: dp
  Hex_Digit_Display hex_digit_display_6 (.value(alu8_1_x[7:4]));  // open: dp
  alu8 alu8_1 (
    .A(rom_1_data[31:24]), .B(rom_1_data[23:16]), .X(alu8_1_x), .Cout(alu8_1_cout), .NZ(alu8_1_nz),
    .S(rom_1_data[7:4]), .OV(alu8_1_ov));
  Hex_Digit_Display hex_digit_display_7 (.value(alu8_1_x[3:0]));  // open: dp
  Comparator comparator_2 (.a(rom_1_data[15:8]), .b(alu8_1_x), .eq(comparator_2_eq));  // open: gt, lt
  Comparator #(.width(1)) comparator_3 (.a(alu8_1_cout), .b(rom_1_data[2]), .eq(comparator_3_eq));  // open: gt, lt
  Comparator #(.width(1)) comparator_4 (.a(alu8_1_nz), .b(rom_1_data[0]), .eq(comparator_4_eq));  // open: gt, lt
  Comparator #(.width(1)) comparator_5 (.a(alu8_1_ov), .b(rom_1_data[1]), .eq(comparator_5_eq));  // open: gt, lt
  or or_1 (or_1_out, comparator_3_eq, rom_1_data[7]);
  not not_1 (not_1_out, and_1_out);
  and and_1 (and_1_out, comparator_2_eq, or_1_out, comparator_4_eq, comparator_5_eq);
  LED led_1 (.in(and_1_out));
  Counter counter_2 (
    .D({8{1'b0}}), .count(not_1_out), .Q(counter_2_q), .clk(CK_out), .clr(comparator_1_eq));  // open: load, carry
  Hex_Digit_Display hex_digit_display_8 (.value(counter_2_q[7:4]));  // open: dp
  D_Flip_Flop d_ff_1 (.clk(CK_out), .D(not_1_out), .Q(d_ff_1_q), .en(not_1_out));  // open: Qn, preset, reset
  Hex_Digit_Display hex_digit_display_9 (.value(counter_2_q[3:0]));  // open: dp
  LED led_2 (.in(d_ff_1_q));

  // Notes on the sheet:
  //   contents of rom_1 (hex, n*v repeats v):
  //   1010221 3010421 7010821 f011021 1f012021 3f014021 7f018023 ff010024 7f018023 7f038023 7f078023
  //   7f0f8023 7f1f8023 7f3f8023 7f7f8023 7fff8023
  //   0: 加算
  //   1: 減算
  //   2: 1加算
  //   3: 1減算
  //   S入力
  //   A入力
  //   8: Bの否定
  //   9: 論理積
  //   14: 論理和
  //   15: 排他的論理和
  //   B入力
  //   X出力
  //   エラーの数
  //   エラー発生時赤に点灯
endmodule

module test_alu_dec (
);

  wire alu8_1_cout, alu8_1_nz, alu8_1_ov, and_1_out, CK_out, comparator_1_eq, comparator_2_eq,
       comparator_3_eq, comparator_4_eq, comparator_5_eq, d_ff_1_q, not_1_out, or_1_out;
  wire [7:0] alu8_1_x, counter_2_q;
  wire [9:0] adder_1_out, counter_1_q;
  wire [31:0] rom_1_data;

  Clock CK (.out(CK_out));
  Counter #(.width(10), .max('h3ff)) counter_1 (
    .D(adder_1_out), .Q(counter_1_q), .clk(CK_out), .clr(comparator_1_eq));  // open: load, count, carry
  Adder #(.width(10)) adder_1 (.a(10'h1), .b(counter_1_q), .out(adder_1_out));  // open: cin, cout
  Comparator #(.width(10)) comparator_1 (.a(adder_1_out), .b(10'h12), .eq(comparator_1_eq));  // open: gt, lt
  ROM #(.addrWidth(10), .dataWidth(32)) rom_1 (.addr(counter_1_q), .data(rom_1_data));  // open: sel
  Hex_Digit_Display hex_digit_display_1 (.value(rom_1_data[7:4]));  // open: dp
  Hex_Digit_Display hex_digit_display_2 (.value(rom_1_data[27:24]));  // open: dp
  Hex_Digit_Display hex_digit_display_3 (.value(rom_1_data[31:28]));  // open: dp
  Hex_Digit_Display hex_digit_display_4 (.value(rom_1_data[19:16]));  // open: dp
  Hex_Digit_Display hex_digit_display_5 (.value(rom_1_data[23:20]));  // open: dp
  Hex_Digit_Display hex_digit_display_6 (.value(alu8_1_x[7:4]));  // open: dp
  alu8 alu8_1 (
    .A(rom_1_data[31:24]), .B(rom_1_data[23:16]), .X(alu8_1_x), .Cout(alu8_1_cout), .NZ(alu8_1_nz),
    .S(rom_1_data[7:4]), .OV(alu8_1_ov));
  Hex_Digit_Display hex_digit_display_7 (.value(alu8_1_x[3:0]));  // open: dp
  Comparator comparator_2 (.a(rom_1_data[15:8]), .b(alu8_1_x), .eq(comparator_2_eq));  // open: gt, lt
  Comparator #(.width(1)) comparator_3 (.a(alu8_1_cout), .b(rom_1_data[2]), .eq(comparator_3_eq));  // open: gt, lt
  Comparator #(.width(1)) comparator_4 (.a(alu8_1_nz), .b(rom_1_data[0]), .eq(comparator_4_eq));  // open: gt, lt
  Comparator #(.width(1)) comparator_5 (.a(alu8_1_ov), .b(rom_1_data[1]), .eq(comparator_5_eq));  // open: gt, lt
  or or_1 (or_1_out, comparator_3_eq, rom_1_data[7]);
  not not_1 (not_1_out, and_1_out);
  LED led_1 (.in(and_1_out));
  and and_1 (and_1_out, comparator_2_eq, or_1_out, comparator_4_eq, comparator_5_eq);
  Counter counter_2 (
    .D({8{1'b0}}), .count(not_1_out), .Q(counter_2_q), .clk(CK_out), .clr(comparator_1_eq));  // open: load, carry
  Hex_Digit_Display hex_digit_display_8 (.value(counter_2_q[7:4]));  // open: dp
  D_Flip_Flop d_ff_1 (.clk(CK_out), .D(not_1_out), .Q(d_ff_1_q), .en(not_1_out));  // open: Qn, preset, reset
  Hex_Digit_Display hex_digit_display_9 (.value(counter_2_q[3:0]));  // open: dp
  LED led_2 (.in(d_ff_1_q));

  // Notes on the sheet:
  //   contents of rom_1 (hex, n*v repeats v):
  //   1010034 3010235 7010635 f010e35 1f011e35 3f013e35 7f017e35 ff01fe35 7f017e35 7f037e35 7f077e35
  //   7f0f7e35 7f1f7e35 7f3f7e35 7f7f7e35 7fff7e35
  //   0: 加算
  //   1: 減算
  //   2: 1加算
  //   3: 1減算
  //   S入力
  //   A入力
  //   8: Bの否定
  //   9: 論理積
  //   14: 論理和
  //   15: 排他的論理和
  //   B入力
  //   X出力
  //   エラーの数
  //   エラー発生時赤に点灯
endmodule

module test_alu_logic (
);

  wire alu8_1_cout, alu8_1_nz, alu8_1_ov, and_1_out, CK_out, comparator_1_eq, comparator_2_eq,
       comparator_3_eq, comparator_4_eq, comparator_5_eq, d_ff_1_q, not_1_out, or_1_out;
  wire [7:0] alu8_1_x, counter_2_q;
  wire [9:0] adder_1_out, counter_1_q;
  wire [31:0] rom_1_data;

  Clock CK (.out(CK_out));
  Counter #(.width(10), .max('h3ff)) counter_1 (
    .D(adder_1_out), .Q(counter_1_q), .clk(CK_out), .clr(comparator_1_eq));  // open: load, count, carry
  Adder #(.width(10)) adder_1 (.a(10'h1), .b(counter_1_q), .out(adder_1_out));  // open: cin, cout
  Comparator #(.width(10)) comparator_1 (.a(adder_1_out), .b(10'h82), .eq(comparator_1_eq));  // open: gt, lt
  ROM #(.addrWidth(10), .dataWidth(32)) rom_1 (.addr(counter_1_q), .data(rom_1_data));  // open: sel
  Hex_Digit_Display hex_digit_display_1 (.value(rom_1_data[7:4]));  // open: dp
  Hex_Digit_Display hex_digit_display_2 (.value(rom_1_data[27:24]));  // open: dp
  Hex_Digit_Display hex_digit_display_3 (.value(rom_1_data[31:28]));  // open: dp
  Hex_Digit_Display hex_digit_display_4 (.value(rom_1_data[19:16]));  // open: dp
  Hex_Digit_Display hex_digit_display_5 (.value(rom_1_data[23:20]));  // open: dp
  Hex_Digit_Display hex_digit_display_6 (.value(alu8_1_x[7:4]));  // open: dp
  alu8 alu8_1 (
    .A(rom_1_data[31:24]), .B(rom_1_data[23:16]), .X(alu8_1_x), .Cout(alu8_1_cout), .NZ(alu8_1_nz),
    .S(rom_1_data[7:4]), .OV(alu8_1_ov));
  Hex_Digit_Display hex_digit_display_7 (.value(alu8_1_x[3:0]));  // open: dp
  Comparator comparator_2 (.a(rom_1_data[15:8]), .b(alu8_1_x), .eq(comparator_2_eq));  // open: gt, lt
  Comparator #(.width(1)) comparator_3 (.a(alu8_1_cout), .b(rom_1_data[2]), .eq(comparator_3_eq));  // open: gt, lt
  Comparator #(.width(1)) comparator_4 (.a(alu8_1_nz), .b(rom_1_data[0]), .eq(comparator_4_eq));  // open: gt, lt
  Comparator #(.width(1)) comparator_5 (.a(alu8_1_ov), .b(rom_1_data[1]), .eq(comparator_5_eq));  // open: gt, lt
  or or_1 (or_1_out, comparator_3_eq, rom_1_data[7]);
  not not_1 (not_1_out, and_1_out);
  and and_1 (and_1_out, comparator_2_eq, or_1_out, comparator_4_eq, comparator_5_eq);
  LED led_1 (.in(and_1_out));
  Counter counter_2 (
    .D({8{1'b0}}), .count(not_1_out), .Q(counter_2_q), .clk(CK_out), .clr(comparator_1_eq));  // open: load, carry
  Hex_Digit_Display hex_digit_display_8 (.value(counter_2_q[7:4]));  // open: dp
  D_Flip_Flop d_ff_1 (.clk(CK_out), .D(not_1_out), .Q(d_ff_1_q), .en(not_1_out));  // open: Qn, preset, reset
  Hex_Digit_Display hex_digit_display_9 (.value(counter_2_q[3:0]));  // open: dp
  LED led_2 (.in(d_ff_1_q));

  // Notes on the sheet:
  //   contents of rom_1 (hex, n*v repeats v):
  //   ff00ff81 ff01fe81 ff03fc81 ff07f881 ff0ff081 ff1fe081 ff3fc081 ff7f8081 ffff0080 ff0080 1ff0080
  //   3ff0080 7ff0080 fff0080 1fff0080 3fff0080 7fff0080 ffff0080 90 10090 30090 70090 f0090 1f0090 3f0090
  //   7f0090 ff0090 90 1000090 3000090 7000090 f000090 1f000090 3f000090 7f000090 ff000090 ff000090
  //   ff010191 ff030391 ff070791 ff0f0f91 ff1f1f91 ff3f3f91 ff7f7f91 ffffff91 ff0090 1ff0191 3ff0391
  //   7ff0791 fff0f91 1fff1f91 3fff3f91 7fff7f91 ffffff91 e0 101e1 303e1 707e1 f0fe1 1f1fe1 3f3fe1 7f7fe1
  //   ffffe1 e0 10001e1 30003e1 70007e1 f000fe1 1f001fe1 3f003fe1 7f007fe1 ff00ffe1 ff00ffe1 ff01ffe1
  //   ff03ffe1 ff07ffe1 ff0fffe1 ff1fffe1 ff3fffe1 ff7fffe1 ffffffe1 ffffe1 1ffffe1 3ffffe1 7ffffe1
  //   fffffe1 1fffffe1 3fffffe1 7fffffe1 ffffffe1 f0 101f1 303f1 707f1 f0ff1 1f1ff1 3f3ff1 7f7ff1 fffff1
  //   f0 10001f1 30003f1 70007f1 f000ff1 1f001ff1 3f003ff1 7f007ff1 ff00fff1 ff00fff1 ff01fef1 ff03fcf1
  //   ff07f8f1 ff0ff0f1 ff1fe0f1 ff3fc0f1 ff7f80f1 ffff00f0 fffff1 1fffef1 3fffcf1 7fff8f1 ffff0f1
  //   1fffe0f1 3fffc0f1 7fff80f1 ffff00f0
  //   0: 加算
  //   1: 減算
  //   2: 1加算
  //   3: 1減算
  //   S入力
  //   A入力
  //   8: Bの否定
  //   9: 論理積
  //   14: 論理和
  //   15: 排他的論理和
  //   B入力
  //   X出力
  //   エラーの数
  //   エラー発生時赤に点灯
endmodule

module FA (
  input  Cin,
  input  A,
  input  B,
  output Sum,
  output Cout
);

  wire nand_1_out, nand_2_out, nand_3_out, xor_1_out;

  xor xor_1 (xor_1_out, A, B);
  nand nand_1 (nand_1_out, Cin, A);
  nand nand_2 (nand_2_out, Cin, B);
  nand nand_3 (nand_3_out, A, B);
  xor xor_2 (Sum, Cin, xor_1_out);
  nand nand_4 (Cout, nand_1_out, nand_2_out, nand_3_out);
endmodule

module alu1 (
  input  A,
  input  B,
  input  Cin,
  input  S10,
  input  S20,
  input  S21,
  output X,
  output Cout,
  output B_prime
);

  wire and_1_out, fa_1_sum, not_1_out, or_1_out, xor_1_out;

  not not_1 (not_1_out, B);
  and and_1 (and_1_out, A, B);
  or or_1 (or_1_out, A, B);
  xor xor_1 (xor_1_out, A, B);
  Multiplexer #(.enable("false")) multiplexer_1 (.in0(B), .in1(not_1_out), .out(B_prime), .sel(S10));
  FA fa_1 (.Cin(Cin), .Sum(fa_1_sum), .A(A), .B(B_prime), .Cout(Cout));
  Multiplexer #(.select(2), .enable("false")) multiplexer_2 (
    .in0(and_1_out), .in1(or_1_out), .in2(xor_1_out), .in3(fa_1_sum), .out(X), .sel({S21, S20}));

  // Notes on the sheet:
  //   M1
  //   M2
endmodule

module sel_dec (
  input  S0,
  input  S1,
  input  S2,
  input  S3,
  output Cin,
  output S10,
  output S40,
  output S20,
  output S21,
  output S30,
  output S50
);

  wire _1_out, _2_out, _3_out, _4_out, _5_out, _6_out, _7_out, _8_out, not_1_out, not_2_out, not_3_out,
       not_4_out;

  not not_1 (not_1_out, S0);
  not not_2 (not_2_out, S1);
  not not_3 (not_3_out, S2);
  not not_4 (not_4_out, S3);
  and _1 (_1_out, not_1_out, not_2_out, not_3_out, not_4_out);
  and _2 (_2_out, S0, not_2_out, not_3_out, not_4_out);
  and _3 (_3_out, not_1_out, S1, not_3_out, not_4_out);
  and _4 (_4_out, S0, S1, not_3_out, not_4_out);
  and _5 (_5_out, not_1_out, not_2_out, not_3_out, S3);
  and _6 (_6_out, S0, not_2_out, not_3_out, S3);
  and _7 (_7_out, not_1_out, S1, S2, S3);
  and _8 (_8_out, S0, S1, S2, S3);
  or or_1 (Cin, _2_out, _4_out);
  or or_2 (S10, _2_out, _4_out, _5_out);
  or or_3 (S40, _1_out, _2_out, _3_out, _4_out, _6_out, _7_out, _8_out);
  or or_4 (S20, _1_out, _2_out, _3_out, _4_out, _5_out, _7_out);
  or or_5 (S21, _1_out, _2_out, _3_out, _4_out, _5_out, _8_out);
  or or_6 (S30, _3_out, _4_out);
  or or_7 (S50, _5_out, _6_out, _7_out, _8_out);
endmodule
